// Logisim project Circuito-MultiCore.circ as structural Verilog
module Main2 (
);

  wire and_1_out, and_2_out, and_3_out, and_4_out, and_5_out, and_6_out, clk, Core1_busy, Core1_exception,
       Core1_syscall, CoreTwo_busy, CoreTwo_exception, CoreTwo_syscall, ER1, ER2, ES1, ES2,
       multiplexer_2_out, multiplexer_3_out, not_1_out, not_2_out, not_3_out, not_4_out, not_5_out,
       not_6_out, not_7_out, not_8_out, or_1_out, ResetFromExcept2_out, ResetFromExcept_out;
  wire [1:0] Destiny;
  wire [13:0] Addr1, Addr2, address_balancer_1_finaladdrc1, address_balancer_1_finaladdrc2,
       multiplexer_1_out, register_1_q, register_2_q;
  wire [31:0] Data1, Data2, demultiplexer_1_out1, demultiplexer_1_out2, MemOutput, multiplexer_4_out;

  Clock clock_1 (.out(clk));
  and and_1 (and_1_out, or_1_out, not_2_out);
  not not_1 (not_1_out, and_4_out);
  and and_2 (and_2_out, not_1_out, clk);
  and and_3 (and_3_out, clk, and_1_out);
  and and_4 (and_4_out, not_3_out, Core1_busy);
  Demultiplexer #(.select(2), .width(32)) demultiplexer_1 (
    .out1(demultiplexer_1_out1), .out2(demultiplexer_1_out2), .in(MemOutput), .sel(Destiny));  // open: out0, out3
  not not_2 (not_2_out, and_5_out);
  not not_3 (not_3_out, not_6_out);
  Button ResetFromExcept (.out(ResetFromExcept_out));
  LED Syscall1 (.in(Core1_syscall));
  LED Exception1 (.in(Core1_exception));
  Button ResetFromExcept2 (.out(ResetFromExcept2_out));
  LED Syscall2 (.in(CoreTwo_syscall));
  LED Exception2 (.in(CoreTwo_exception));
  and and_5 (and_5_out, CoreTwo_busy, not_4_out);
  Core Core1 (
    .Clock(and_2_out), .DataInput(demultiplexer_1_out1), .OutsideReset(ResetFromExcept_out),
    .Busy(Core1_busy), .SysCall(Core1_syscall), .Data(Data1), .Addrs(Addr1), .EnableStore(ES1),
    .EnableRead(ER1), .Exception(Core1_exception));
  Core2 CoreTwo (
    .Clock(and_3_out), .DataInput(demultiplexer_1_out2), .OutsideReset(ResetFromExcept2_out),
    .Busy(CoreTwo_busy), .SysCall(CoreTwo_syscall), .Data(Data2), .Addrs(Addr2), .EnableStore(ES2),
    .EnableRead(ER2), .Exception(CoreTwo_exception));
  not not_4 (not_4_out, not_8_out);
  or or_1 (or_1_out, not_7_out, not_5_out, Destiny[1]);
  not not_5 (not_5_out, CoreTwo_busy);
  not not_6 (not_6_out, Destiny[1]);
  not not_7 (not_7_out, Core1_busy);
  and and_6 (and_6_out, not_7_out, CoreTwo_busy);
  Register #(.width(14)) register_1 (.D(Addr1), .Q(register_1_q), .clk(clk));  // open: en, clr
  Register #(.width(14)) register_2 (.D(Addr2), .Q(register_2_q), .clk(clk));  // open: en, clr
  Register #(.width(1)) Core1Owner (.D(Core1_busy), .en(not_6_out), .clk(clk), .Q(Destiny[0]));  // open: clr
  not not_8 (not_8_out, Destiny[0]);
  Register #(.width(1)) register_3 (.D(and_6_out), .en(not_8_out), .clk(clk), .Q(Destiny[1]));  // open: clr
  address_balancer address_balancer_1 (
    .addrC1(register_1_q), .addrC2(register_2_q), .finalAddrC1(address_balancer_1_finaladdrc1),
    .finalAddrC2(address_balancer_1_finaladdrc2));
  Multiplexer #(.select(2), .width(14)) multiplexer_1 (
    .in1(address_balancer_1_finaladdrc1), .in2(address_balancer_1_finaladdrc2), .out(multiplexer_1_out),
    .sel(Destiny));  // open: in0, in3
  Multiplexer #(.select(2)) multiplexer_2 (
    .in1(ES1), .in2(ES2), .out(multiplexer_2_out), .sel(Destiny));  // open: in0, in3
  Multiplexer #(.select(2)) multiplexer_3 (
    .in1(ER1), .in2(ER2), .out(multiplexer_3_out), .sel(Destiny));  // open: in0, in3
  Multiplexer #(.select(2), .width(32)) multiplexer_4 (
    .in1(Data1), .in2(Data2), .out(multiplexer_4_out), .sel(Destiny));  // open: in0, in3
  RAM #(.addrWidth(14), .dataWidth(32)) ram_1 (
    .addr(multiplexer_1_out), .we(multiplexer_2_out), .oe(multiplexer_3_out), .clk(clk),
    .din(multiplexer_4_out), .dout(MemOutput));
endmodule

module Core (
  input  OutsideReset,
  input  Clock,
  input  [31:0] DataInput,
  output Busy,
  output SysCall,
  output Exception,
  output [13:0] Addrs,
  output EnableStore,
  output EnableRead,
  output [31:0] Data
);

  wire and_1_out, and_3_out, and_7_out, and_8_out, and_11_out, and_12_out, and_13_out, and_14_out,
       and_15_out, branch_taken, bTaken, busy_t, BusyDa1, BusyIn1, cache_datos_1_ram_write, can_write_ra,
       can_write_ra1_q, can_write_ra2_q, comparator_1_gt, comparator_2_eq, comparator_3_eq, comparator_4_eq,
       comparator_5_eq, comparator_6_gt, comparator_7_eq, comparator_8_eq, comparator_9_eq, comparator_10_eq,
       comparator_13_eq, comparator_14_gt, comparator_15_eq, comparator_16_eq, counter_2_q, counter_3_q,
       decoder_1_out14, decoder_1_out15, decoder_1_out20, decoder_2_out12, decoder_2_out13, decoder_2_out14,
       decoder_2_out15, decoder_2_out20, HitD, HitI, InvalidAddressExc, load_enable, manual_reset,
       manual_reset_out, MissD, MissI, multiplexer_3_out, not_1_out, not_2_out, not_3_out, not_4_out,
       not_5_out, not_6_out, not_7_out, not_8_out, not_9_out, not_10_out, not_11_out, not_12_out, not_13_out,
       not_14_out, or_1_out, or_2_out, or_3_out, or_4_out, or_6_out, or_7_out, or_8_out, or_9_out, or_10_out,
       or_11_out, or_12_out, or_13_out, or_14_out, or_15_out, ram_read_enable_d, ram_read_enable_i,
       ram_write_enable, register_1_q, register_2_q, RewritePC, S_data_des, stop_cache_D, store_enable, Write;
  wire [2:0] InstFetch_q_3;
  wire [4:0] Destino, Destino2_q, Destino3_q, InstFetch_q_2, InstFetch_q_4, InstFetch_q_5, mem_OpCode_q,
       OpCode2_q, OpCode3_q, S_dest, translator_1_translatedc;
  wire [6:0] InstFetch_q, InstFetch_q_6;
  wire [11:0] jalr_offset_q;
  wire [12:0] branch_offset_q, multiplier_2_out;
  wire [13:0] addr_calculator_1_addr, addr_in, addr_ram_in_d, addr_ram_in_i, branch_jump_1_next_pc,
       cache_datos_1_ram_address, counter_1_q, PC_Actual, register_3_q, register_4_q;
  wire [20:0] multiplier_1_out, register_9_q;
  wire [31:0] base_position, cache_datos_1_ram_return_data, cache_instrucciones_1_cpu_instruction,
       Instruction01_q, load_offset, load_result, mem_Resultado_q, ModifiedPC, multiplexer_1_out,
       multiplexer_4_out, multiplexer_5_out, multiplexer_7_out, multiplexer_8_out, multiplexer_9_out,
       multiplexer_10_out, multiplexer_11_out, multiplexer_12_out, multiplexer_13_out, multiplexer_14_out,
       multiplexer_15_out, NewPC, Op2_q, ram_data_in_d, ram_data_in_i, register_11_q, register_12_q,
       Registers_op1, Resultado_q, return_address, return_address1_q, return_address2_q, store_offset,
       store_write_data, store_write_in, WriteData;

  LED InvalidInstruction (.in(and_1_out));
  and and_1 (and_1_out, ram_read_enable_i, not_1_out, Addrs[13]);
  not not_1 (not_1_out, stop_cache_D);
  or or_1 (or_1_out, and_1_out, and_3_out);
  Multiplexer #(.width(32)) multiplexer_1 (.in0(NewPC), .in1(ModifiedPC), .out(multiplexer_1_out), .sel(branch_taken));
  and and_2 (InvalidAddressExc, or_1_out, busy_t);
  Multiplexer #(.width(14)) multiplexer_2 (.in0(addr_ram_in_i), .in1(addr_ram_in_d), .out(Addrs), .sel(stop_cache_D));
  or or_2 (or_2_out, ram_write_enable, ram_read_enable_d);
  or or_3 (or_3_out, ram_read_enable_i, ram_read_enable_d);
  not not_2 (not_2_out, InvalidAddressExc);
  LED led_1 (.in(SysCall));
  LED InvalidData (.in(and_3_out));
  and and_3 (and_3_out, stop_cache_D, not_3_out, or_2_out);
  not not_3 (not_3_out, Addrs[13]);
  and and_4 (EnableStore, Addrs[13], stop_cache_D, ram_write_enable);
  and and_5 (EnableRead, or_3_out, not_2_out);
  Multiplexer multiplexer_3 (.in0(RewritePC), .in1(branch_taken), .out(multiplexer_3_out), .sel(branch_taken));
  Counter #(.max('h3fff), .width(14)) counter_1 (
    .clr(Exception), .load(multiplexer_3_out), .count(not_5_out), .clk(Clock), .D(multiplexer_1_out[13:0]),
    .Q(counter_1_q));  // open: up, carry
  LED exception_flag (.in(Exception));
  Register #(.width(1)) register_1 (.D(BusyDa1), .clk(Clock), .Q(register_1_q));  // open: en, clr
  Demultiplexer #(.width(32)) demultiplexer_1 (
    .out0(ram_data_in_i), .out1(ram_data_in_d), .in(DataInput), .sel(stop_cache_D));
  Button u_manual_reset (.out(manual_reset_out));
  Counter #(.max('h1), .ongoal("stay"), .width(1)) counter_2 (
    .Q(counter_2_q), .clk(MissD), .clr(HitD));  // open: load, D, count, carry, up
  and and_6 (manual_reset, Exception, or_4_out);
  or or_4 (or_4_out, manual_reset_out, OutsideReset);
  or or_5 (busy_t, BusyIn1, register_1_q);
  and and_7 (and_7_out, Clock, not_4_out);
  and and_8 (and_8_out, Clock, or_6_out);
  or or_6 (or_6_out, store_enable, load_enable);
  not not_4 (not_4_out, stop_cache_D);
  not not_5 (not_5_out, or_7_out);
  or or_7 (or_7_out, BusyIn1, Exception, bTaken, stop_cache_D);
  Counter #(.max('h1), .ongoal("stay"), .width(1)) counter_3 (
    .Q(counter_3_q), .clk(MissI), .clr(HitI));  // open: load, D, count, carry, up
  or or_8 (or_8_out, counter_3_q, counter_2_q);
  cache_instrucciones cache_instrucciones_1 (
    .clk(and_7_out), .reset(Exception), .cpu_address(counter_1_q), .cpu_read(1'b1), .cpu_enable(1'b1),
    .ram_data_to_write(ram_data_in_i), .monitor_enable(1'b1),
    .cpu_instruction(cache_instrucciones_1_cpu_instruction), .ram_address(addr_ram_in_i),
    .ram_read(ram_read_enable_i), .cache_hit(HitI), .cache_miss(MissI), .busy(BusyIn1));
  LED led_2 (.in(HitI));
  LED led_3 (.in(MissI));
  LED led_4 (.in(BusyIn1));
  Register #(.width(1)) register_2 (.D(MissI), .en(not_6_out), .clk(Clock), .Q(register_2_q), .clr(Exception));
  not not_6 (not_6_out, register_2_q);
  and and_9 (Busy, or_8_out, busy_t);
  or or_9 (or_9_out, HitI, MissI);
  cache_datos cache_datos_1 (
    .clk(and_8_out), .reset(Exception), .cpu_asked_address(addr_in), .cpu_data_to_write(store_write_in),
    .cpu_write(store_enable), .cpu_read(load_enable), .cpu_enable(1'b1), .ram_data_to_write(ram_data_in_d),
    .monitor_enable(1'b1), .cpu_return_data(load_result), .ram_address(cache_datos_1_ram_address),
    .ram_return_data(cache_datos_1_ram_return_data), .ram_write(cache_datos_1_ram_write),
    .ram_read(ram_read_enable_d), .cache_hit(HitD), .cache_miss(MissD), .busy(BusyDa1));
  LED led_5 (.in(HitD));
  LED led_6 (.in(MissD));
  LED led_7 (.in(BusyDa1));
  or or_10 (or_10_out, ram_read_enable_d, store_enable, load_enable, ram_write_enable);
  Multiplexer #(.width(32)) multiplexer_4 (
    .in0({32{1'b0}}), .in1(cache_instrucciones_1_cpu_instruction), .out(multiplexer_4_out), .sel(or_9_out));
  Multiplexer #(.width(32)) multiplexer_5 (
    .in0({32{1'b0}}), .in1(multiplexer_4_out), .out(multiplexer_5_out), .sel(register_2_q));
  and and_10 (stop_cache_D, BusyDa1, or_10_out);
  Register #(.width(14)) register_3 (.D(counter_1_q), .en(not_7_out), .clk(Clock), .Q(register_3_q), .clr(or_11_out));
  Register #(.width(32)) InstFetch (
    .D(multiplexer_5_out), .en(not_7_out), .clk(Clock),
    .Q({InstFetch_q_6, InstFetch_q_5, InstFetch_q_4, InstFetch_q_3, InstFetch_q_2, InstFetch_q}),
    .clr(or_11_out));
  not not_7 (not_7_out, stop_cache_D);
  or or_11 (or_11_out, Exception, branch_taken);
  Comparator #(.mode("unsigned"), .width(5)) comparator_1 (
    .a(Destino2_q), .b({5{1'b0}}), .gt(comparator_1_gt));  // open: eq, lt
  Comparator #(.width(7)) comparator_2 (.a(InstFetch_q), .b({7{1'b0}}), .eq(comparator_2_eq));  // open: gt, lt
  Comparator #(.mode("unsigned"), .width(5)) comparator_3 (
    .a(InstFetch_q_4), .b(Destino2_q), .eq(comparator_3_eq));  // open: gt, lt
  Comparator #(.mode("unsigned"), .width(5)) comparator_4 (
    .a(InstFetch_q_5), .b(Destino2_q), .eq(comparator_4_eq));  // open: gt, lt
  Translator translator_1 (
    .clock(Clock), .opCode(InstFetch_q), .funct3(InstFetch_q_3), .funct7(InstFetch_q_6),
    .TranslatedC(translator_1_translatedc));
  Register #(.width(14)) register_4 (
    .D(cache_datos_1_ram_address), .clk(and_8_out), .Q(register_4_q), .clr(Exception));  // open: en
  not not_8 (not_8_out, comparator_2_eq);
  Comparator #(.width(5)) comparator_5 (
    .a({5{1'b1}}), .b(translator_1_translatedc), .eq(comparator_5_eq));  // open: gt, lt
  Registros Registers (
    .writeEnable(Write), .exception(Exception), .clk(Clock), .writeDestiny(Destino), .nOp1(InstFetch_q_4),
    .nOp2(InstFetch_q_5), .writeData(WriteData), .op2(store_write_data), .op1(Registers_op1));
  and and_11 (and_11_out, comparator_3_eq, comparator_1_gt);
  and and_12 (and_12_out, comparator_4_eq, comparator_1_gt);
  Register #(.width(32)) register_5 (
    .D(cache_datos_1_ram_return_data), .clk(and_8_out), .Q(Data), .clr(Exception));  // open: en
  Register #(.width(1)) register_6 (
    .D(cache_datos_1_ram_write), .clk(and_8_out), .Q(ram_write_enable), .clr(Exception));  // open: en
  and and_13 (and_13_out, not_8_out, comparator_5_eq);
  Comparator #(.mode("unsigned"), .width(5)) comparator_6 (
    .a(Destino3_q), .b({5{1'b0}}), .gt(comparator_6_gt));  // open: eq, lt
  Multiplexer #(.width(14)) multiplexer_6 (
    .in0(register_4_q), .in1(cache_datos_1_ram_address), .out(addr_ram_in_d), .sel(load_enable));
  Multiplier #(.width(21)) multiplier_1 (
    .a({1'b0, InstFetch_q_6[6], InstFetch_q_4, InstFetch_q_3, InstFetch_q_5[0], InstFetch_q_6[5:0], InstFetch_q_5[4:1]}),
    .b(21'h2), .out(multiplier_1_out));  // open: cin, cout
  Multiplier #(.width(13)) multiplier_2 (
    .a({InstFetch_q_6[6], InstFetch_q_2[0], InstFetch_q_6[5:0], InstFetch_q_2[4:1], 1'b0}), .b(13'h2),
    .out(multiplier_2_out));  // open: cin, cout
  or or_12 (or_12_out, InvalidAddressExc, and_13_out);
  Comparator #(.mode("unsigned"), .width(5)) comparator_7 (
    .a(InstFetch_q_4), .b(Destino3_q), .eq(comparator_7_eq));  // open: gt, lt
  Comparator #(.mode("unsigned"), .width(5)) comparator_8 (
    .a(InstFetch_q_5), .b(Destino3_q), .eq(comparator_8_eq));  // open: gt, lt
  Register #(.width(1)) register_7 (.D(or_12_out), .en(or_12_out), .clk(Clock), .Q(Exception), .clr(manual_reset));
  and and_14 (and_14_out, comparator_7_eq, comparator_6_gt);
  and and_15 (and_15_out, comparator_8_eq, comparator_6_gt);
  Multiplexer #(.width(32)) multiplexer_7 (
    .in0({{20{1'b0}}, InstFetch_q_6, InstFetch_q_5}),
    .in1({InstFetch_q_6, InstFetch_q_5, InstFetch_q_4, InstFetch_q_3, {12{1'b0}}}), .out(multiplexer_7_out),
    .sel(or_13_out));
  or or_13 (or_13_out, comparator_9_eq, comparator_10_eq);
  Multiplexer #(.width(32)) multiplexer_8 (.in0(Registers_op1), .in1(NewPC), .out(multiplexer_8_out), .sel(and_11_out));
  Multiplexer #(.width(32)) multiplexer_9 (
    .in0(store_write_data), .in1(NewPC), .out(multiplexer_9_out), .sel(and_12_out));
  Comparator #(.width(5)) comparator_9 (
    .a(translator_1_translatedc), .b(5'b10010), .eq(comparator_9_eq));  // open: gt, lt
  Register #(.width(14)) register_8 (.D(register_3_q), .en(not_9_out), .clk(Clock), .Q(PC_Actual), .clr(Exception));
  Multiplexer #(.width(32)) multiplexer_10 (
    .in0(multiplexer_8_out), .in1(Resultado_q), .out(multiplexer_10_out), .sel(and_14_out));
  Multiplexer #(.width(32)) multiplexer_11 (
    .in0(multiplexer_9_out), .in1(Resultado_q), .out(multiplexer_11_out), .sel(and_15_out));
  Comparator #(.width(5)) comparator_10 (
    .a(translator_1_translatedc), .b(5'b10011), .eq(comparator_10_eq));  // open: gt, lt
  Register #(.width(12)) jalr_offset (
    .D({InstFetch_q_6, InstFetch_q_5}), .en(not_9_out), .clk(Clock), .Q(jalr_offset_q), .clr(Exception));
  Register #(.width(21)) register_9 (
    .D(multiplier_1_out), .en(not_9_out), .clk(Clock), .Q(register_9_q), .clr(Exception));
  Register #(.width(13)) branch_offset (
    .D(multiplier_2_out), .en(not_9_out), .clk(Clock), .Q(branch_offset_q), .clr(Exception));
  Register #(.width(32)) Instruction01 (
    .D({InstFetch_q_6, InstFetch_q_5, InstFetch_q_4, InstFetch_q_3, InstFetch_q_2, InstFetch_q}),
    .en(not_9_out), .clk(Clock), .Q({Instruction01_q[31:25], S_dest, Instruction01_q[19:0]}));  // open: clr
  Register #(.width(32)) store_offset_2 (
    .D({{20{1'b0}}, InstFetch_q_6, InstFetch_q_2}), .en(not_9_out), .clk(Clock), .Q(store_offset),
    .clr(Exception));
  Register #(.width(5)) OpCode2 (
    .D(translator_1_translatedc), .en(not_9_out), .clk(Clock), .Q(OpCode2_q), .clr(Exception));
  Register #(.width(5)) Destino2 (.D(InstFetch_q_2), .en(not_9_out), .clk(Clock), .Q(Destino2_q), .clr(Exception));
  Register #(.width(32)) Op1 (.D(multiplexer_10_out), .en(not_9_out), .clk(Clock), .Q(base_position), .clr(Exception));
  Register #(.width(32)) Op2 (.D(multiplexer_11_out), .en(not_9_out), .clk(Clock), .Q(Op2_q), .clr(Exception));
  Register #(.width(32)) Imm2 (.D(multiplexer_7_out), .en(not_9_out), .clk(Clock), .Q(load_offset), .clr(Exception));
  not not_9 (not_9_out, stop_cache_D);
  Comparator #(.mode("unsigned"), .width(5)) comparator_11 (
    .a(OpCode2_q), .b(5'b10011), .eq(RewritePC));  // open: gt, lt
  Multiplexer #(.width(32)) multiplexer_12 (
    .in0(base_position), .in1({{18{1'b0}}, PC_Actual}), .out(multiplexer_12_out), .sel(RewritePC));
  branch_jump branch_jump_1 (
    .opcode(OpCode2_q), .op1(base_position), .op2(Op2_q), .branch_offset(branch_offset_q),
    .jump_offset(register_9_q), .jalr_rs1(base_position), .jalr_offset(jalr_offset_q),
    .current_pc(PC_Actual), .rd_write_en(can_write_ra), .rd_data(return_address),
    .next_pc(branch_jump_1_next_pc), .branch_taken(branch_taken));
  assign ModifiedPC = {{18{branch_jump_1_next_pc[13]}}, branch_jump_1_next_pc};  // Bit_Extender bit_extender_1
  Comparator #(.width(5)) comparator_12 (.a(OpCode2_q), .b(5'b10100), .eq(SysCall));  // open: gt, lt
  Register #(.width(1)) register_10 (.D(branch_taken), .clk(Clock), .Q(bTaken));  // open: en, clr
  ALU ALU1 (.opCode(OpCode2_q), .op1(multiplexer_12_out), .op2(Op2_q), .imm(load_offset), .result(NewPC));
  Multiplexer #(.select(5), .width(32)) multiplexer_13 (
    .in0(NewPC), .in1(NewPC), .in2(NewPC), .in3(NewPC), .in4(NewPC), .in5(NewPC), .in6(NewPC), .in7(NewPC),
    .in8(NewPC), .in9(NewPC), .in10(NewPC), .in11(NewPC), .in12({32{1'b0}}), .in13({32{1'b0}}), .in14(NewPC),
    .in15(NewPC), .in16({32{1'b0}}), .in17({32{1'b0}}), .in18(NewPC), .in19({32{1'b0}}), .in20({32{1'b0}}),
    .in21({32{1'b0}}), .in22({32{1'b0}}), .in23({32{1'b0}}), .in24({32{1'b0}}), .in25({32{1'b0}}),
    .in26({32{1'b0}}), .in27({32{1'b0}}), .in28({32{1'b0}}), .in29({32{1'b0}}), .in30({32{1'b0}}),
    .in31({32{1'b0}}), .out(multiplexer_13_out), .sel(OpCode2_q));
  Register #(.width(32)) register_11 (
    .D(store_write_data), .en(not_10_out), .clk(Clock), .Q(register_11_q), .clr(Exception));
  addr_calculator addr_calculator_1 (
    .store_offset(store_offset), .load_offset(load_offset), .op_code_alu(OpCode2_q), .base(base_position),
    .addr(addr_calculator_1_addr));
  Register #(.width(32)) Instruction02 (
    .D({Instruction01_q[31:25], S_dest, Instruction01_q[19:0]}), .en(not_10_out), .clk(Clock));  // open: Q, clr
  Multiplexer #(.width(32)) multiplexer_14 (
    .in0(register_11_q), .in1(WriteData), .out(multiplexer_14_out), .sel(S_data_des));
  Register #(.width(14)) store_addr (
    .D(addr_calculator_1_addr), .en(not_10_out), .clk(Clock), .Q(addr_in), .clr(Exception));
  Register #(.width(5)) OpCode3 (.D(OpCode2_q), .en(not_10_out), .clk(Clock), .Q(OpCode3_q), .clr(Exception));
  Register #(.width(5)) Destino3 (.D(Destino2_q), .en(not_10_out), .clk(Clock), .Q(Destino3_q), .clr(Exception));
  Register #(.width(32)) Resultado (
    .D(multiplexer_13_out), .en(not_10_out), .clk(Clock), .Q(Resultado_q), .clr(Exception));
  Register #(.width(32)) return_address1 (
    .D(return_address), .en(not_10_out), .clk(Clock), .Q(return_address1_q), .clr(Exception));
  Register #(.width(1)) can_write_ra1 (
    .D(can_write_ra), .en(not_10_out), .clk(Clock), .Q(can_write_ra1_q), .clr(Exception));
  not not_10 (not_10_out, stop_cache_D);
  Register #(.width(32)) store_data (
    .D(multiplexer_14_out), .en(not_10_out), .clk(Clock), .Q(store_write_in), .clr(Exception));
  Register #(.width(5)) mem_OpCode (.D(OpCode3_q), .en(not_11_out), .clk(Clock), .Q(mem_OpCode_q), .clr(Exception));
  Register #(.width(5)) mem_Destino (.D(Destino3_q), .en(not_11_out), .clk(Clock), .Q(Destino), .clr(Exception));
  Register #(.width(32)) mem_Resultado (
    .D(Resultado_q), .en(not_11_out), .clk(Clock), .Q(mem_Resultado_q), .clr(Exception));
  Register #(.width(32)) register_12 (
    .D(load_result), .en(not_11_out), .clk(Clock), .Q(register_12_q), .clr(Exception));
  Register #(.width(32)) return_address2 (
    .D(return_address1_q), .en(not_11_out), .clk(Clock), .Q(return_address2_q), .clr(Exception));
  Register #(.width(1)) can_write_ra2 (
    .D(can_write_ra1_q), .en(not_11_out), .clk(Clock), .Q(can_write_ra2_q), .clr(Exception));
  Decoder #(.select(5)) decoder_1 (
    .out12(load_enable), .out13(store_enable), .out14(decoder_1_out14), .out15(decoder_1_out15),
    .out20(decoder_1_out20), .sel(OpCode3_q));  // open: out0, out1, out2, out3, out4, out5, out6, out7, out8, out9, out10, out11, out16, out17, out18, out19, out21, out22, out23, out24, out25, out26, out27, out28, out29, out30, out31, en
  not not_11 (not_11_out, stop_cache_D);
  Multiplexer #(.width(32)) multiplexer_15 (
    .in0(mem_Resultado_q), .in1(register_12_q), .out(multiplexer_15_out), .sel(comparator_13_eq));
  Comparator #(.width(5)) comparator_13 (.a(mem_OpCode_q), .b(5'b01100), .eq(comparator_13_eq));  // open: gt, lt
  Comparator #(.mode("unsigned"), .width(5)) comparator_14 (
    .a(mem_OpCode_q), .b(5'b10100), .gt(comparator_14_gt));  // open: eq, lt
  or or_14 (or_14_out, decoder_1_out20, decoder_1_out15, decoder_1_out14, store_enable, comparator_14_gt);
  Multiplexer #(.width(32)) multiplexer_16 (
    .in0(multiplexer_15_out), .in1(return_address2_q), .out(WriteData), .sel(can_write_ra2_q));
  Decoder #(.select(5)) decoder_2 (
    .out12(decoder_2_out12), .out13(decoder_2_out13), .out14(decoder_2_out14), .out15(decoder_2_out15),
    .out20(decoder_2_out20), .sel(mem_OpCode_q));  // open: out0, out1, out2, out3, out4, out5, out6, out7, out8, out9, out10, out11, out16, out17, out18, out19, out21, out22, out23, out24, out25, out26, out27, out28, out29, out30, out31, en
  not not_12 (not_12_out, or_14_out);
  not not_13 (not_13_out, comparator_15_eq);
  Comparator #(.mode("unsigned"), .width(5)) comparator_15 (
    .a(mem_OpCode_q), .b({5{1'b0}}), .eq(comparator_15_eq));  // open: gt, lt
  Comparator #(.mode("unsigned"), .width(5)) comparator_16 (
    .a(Destino), .b(S_dest), .eq(comparator_16_eq));  // open: gt, lt
  or or_15 (or_15_out, decoder_2_out20, decoder_2_out15, decoder_2_out14, decoder_2_out13, decoder_2_out12);
  not not_14 (not_14_out, or_15_out);
  or or_16 (Write, not_14_out, not_12_out);
  and and_16 (S_data_des, not_12_out, not_13_out, comparator_16_eq);

  // Other names for the same wires on the sheet: ram_data_out[31:0] = Data; SystemCall = SysCall

  // Notes on the sheet:
  //   Cuando se activa indica que hay una syscall
  //   Cuando se activa indica que hay una excepcion
  //   Dependiendo de la instruccion, algo diferente tiene que salir
  //   Registro al que se escribira
  //   Este decoder nos dice si una instruccion escribe en registro
  //   Datos a escribir en registro
  //   Decide si debe escribirse algo en registro
endmodule

module Core2 (
  input  OutsideReset,
  input  Clock,
  input  [31:0] DataInput,
  output Busy,
  output SysCall,
  output Exception,
  output [13:0] Addrs,
  output EnableStore,
  output EnableRead,
  output [31:0] Data
);

  wire and_1_out, and_3_out, and_7_out, and_8_out, and_11_out, and_12_out, and_13_out, and_14_out,
       and_15_out, branch_taken, bTaken, busy_t, BusyDa1, BusyIn1, cache_datos_1_ram_write, can_write_ra,
       can_write_ra1_q, can_write_ra2_q, comparator_1_gt, comparator_2_eq, comparator_3_eq, comparator_4_eq,
       comparator_5_eq, comparator_6_gt, comparator_7_eq, comparator_8_eq, comparator_9_eq, comparator_10_eq,
       comparator_13_eq, comparator_14_gt, comparator_15_eq, comparator_16_eq, counter_2_q, counter_3_q,
       decoder_1_out14, decoder_1_out15, decoder_1_out20, decoder_2_out12, decoder_2_out13, decoder_2_out14,
       decoder_2_out15, decoder_2_out20, HitD, HitI, InvalidAddressExc, load_enable, manual_reset,
       manual_reset_out, MissD, MissI, multiplexer_3_out, not_1_out, not_2_out, not_3_out, not_4_out,
       not_5_out, not_6_out, not_7_out, not_8_out, not_9_out, not_10_out, not_11_out, not_12_out, not_13_out,
       not_14_out, or_1_out, or_2_out, or_3_out, or_4_out, or_6_out, or_7_out, or_8_out, or_9_out, or_10_out,
       or_11_out, or_12_out, or_13_out, or_14_out, or_15_out, or_16_out, ram_read_enable_d,
       ram_read_enable_i, ram_write_enable, register_1_q, register_2_q, RewritePC, S_data_des, stop_cache_D,
       store_enable, Write;
  wire [2:0] InstFetch_q_3;
  wire [4:0] Destino, Destino2_q, Destino3_q, InstFetch_q_2, InstFetch_q_4, InstFetch_q_5, mem_OpCode_q,
       OpCode2_q, OpCode3_q, S_dest, translator_1_translatedc;
  wire [6:0] InstFetch_q, InstFetch_q_6;
  wire [11:0] jalr_offset_q;
  wire [12:0] branch_offset_q, multiplier_2_out;
  wire [13:0] addr_calculator_1_addr, addr_in, addr_ram_in_d, addr_ram_in_i, branch_jump_1_next_pc,
       cache_datos_1_ram_address, counter_1_q, PC_Actual, register_3_q, register_4_q;
  wire [20:0] multiplier_1_out, register_9_q;
  wire [31:0] base_position, cache_datos_1_ram_return_data, cache_instrucciones_1_cpu_instruction,
       Instruction01_q, load_offset, load_result, mem_Resultado_q, ModifiedPC, multiplexer_1_out,
       multiplexer_4_out, multiplexer_5_out, multiplexer_7_out, multiplexer_8_out, multiplexer_9_out,
       multiplexer_10_out, multiplexer_11_out, multiplexer_12_out, multiplexer_13_out, multiplexer_14_out,
       multiplexer_15_out, NewPC, Op2_q, ram_data_in_d, ram_data_in_i, register_11_q, Registers_op1,
       Resultado_q, return_address, return_address1_q, return_address2_q, store_offset, store_write_data,
       store_write_in, WriteData;

  LED InvalidInstruction (.in(and_1_out));
  and and_1 (and_1_out, ram_read_enable_i, not_1_out, Addrs[13]);
  not not_1 (not_1_out, stop_cache_D);
  or or_1 (or_1_out, and_1_out, and_3_out);
  Multiplexer #(.width(32)) multiplexer_1 (.in0(NewPC), .in1(ModifiedPC), .out(multiplexer_1_out), .sel(branch_taken));
  and and_2 (InvalidAddressExc, or_1_out, busy_t);
  Multiplexer #(.width(14)) multiplexer_2 (.in0(addr_ram_in_i), .in1(addr_ram_in_d), .out(Addrs), .sel(stop_cache_D));
  or or_2 (or_2_out, ram_write_enable, ram_read_enable_d);
  or or_3 (or_3_out, ram_read_enable_i, ram_read_enable_d);
  not not_2 (not_2_out, InvalidAddressExc);
  LED led_1 (.in(SysCall));
  LED InvalidData (.in(and_3_out));
  and and_3 (and_3_out, stop_cache_D, not_3_out, or_2_out);
  not not_3 (not_3_out, Addrs[13]);
  and and_4 (EnableStore, Addrs[13], stop_cache_D, ram_write_enable);
  and and_5 (EnableRead, or_3_out, not_2_out);
  Multiplexer multiplexer_3 (.in0(RewritePC), .in1(branch_taken), .out(multiplexer_3_out), .sel(branch_taken));
  Counter #(.max('h3fff), .width(14)) counter_1 (
    .clr(Exception), .load(multiplexer_3_out), .count(not_5_out), .clk(Clock), .D(multiplexer_1_out[13:0]),
    .Q(counter_1_q));  // open: up, carry
  LED exception_flag (.in(Exception));
  Register #(.width(1)) register_1 (.D(BusyDa1), .clk(Clock), .Q(register_1_q));  // open: en, clr
  Demultiplexer #(.width(32)) demultiplexer_1 (
    .out0(ram_data_in_i), .out1(ram_data_in_d), .in(DataInput), .sel(stop_cache_D));
  Button u_manual_reset (.out(manual_reset_out));
  Counter #(.max('h1), .ongoal("stay"), .width(1)) counter_2 (
    .Q(counter_2_q), .clk(MissD), .clr(HitD));  // open: load, D, count, carry, up
  and and_6 (manual_reset, Exception, or_4_out);
  or or_4 (or_4_out, manual_reset_out, OutsideReset);
  or or_5 (busy_t, BusyIn1, register_1_q);
  and and_7 (and_7_out, Clock, not_4_out);
  and and_8 (and_8_out, Clock, or_6_out);
  or or_6 (or_6_out, store_enable, load_enable);
  not not_4 (not_4_out, stop_cache_D);
  not not_5 (not_5_out, or_7_out);
  or or_7 (or_7_out, BusyIn1, Exception, bTaken, stop_cache_D);
  Counter #(.max('h1), .ongoal("stay"), .width(1)) counter_3 (
    .Q(counter_3_q), .clk(MissI), .clr(HitI));  // open: load, D, count, carry, up
  or or_8 (or_8_out, counter_3_q, counter_2_q);
  cache_instrucciones cache_instrucciones_1 (
    .clk(and_7_out), .reset(Exception), .cpu_address(counter_1_q), .cpu_read(1'b1), .cpu_enable(1'b1),
    .ram_data_to_write(ram_data_in_i), .monitor_enable(1'b1),
    .cpu_instruction(cache_instrucciones_1_cpu_instruction), .ram_address(addr_ram_in_i),
    .ram_read(ram_read_enable_i), .cache_hit(HitI), .cache_miss(MissI), .busy(BusyIn1));
  LED led_2 (.in(HitI));
  LED led_3 (.in(MissI));
  LED led_4 (.in(BusyIn1));
  Register #(.width(1)) register_2 (.D(MissI), .en(not_6_out), .clk(Clock), .Q(register_2_q), .clr(Exception));
  not not_6 (not_6_out, register_2_q);
  and and_9 (Busy, or_8_out, busy_t);
  or or_9 (or_9_out, HitI, MissI);
  cache_datos cache_datos_1 (
    .clk(and_8_out), .reset(Exception), .cpu_asked_address(addr_in), .cpu_data_to_write(store_write_in),
    .cpu_write(store_enable), .cpu_read(load_enable), .cpu_enable(1'b1), .ram_data_to_write(ram_data_in_d),
    .monitor_enable(1'b1), .cpu_return_data(load_result), .ram_address(cache_datos_1_ram_address),
    .ram_return_data(cache_datos_1_ram_return_data), .ram_write(cache_datos_1_ram_write),
    .ram_read(ram_read_enable_d), .cache_hit(HitD), .cache_miss(MissD), .busy(BusyDa1));
  LED led_5 (.in(HitD));
  LED led_6 (.in(MissD));
  LED led_7 (.in(BusyDa1));
  or or_10 (or_10_out, ram_read_enable_d, store_enable, load_enable, ram_write_enable);
  Multiplexer #(.width(32)) multiplexer_4 (
    .in0({32{1'b0}}), .in1(cache_instrucciones_1_cpu_instruction), .out(multiplexer_4_out), .sel(or_9_out));
  Multiplexer #(.width(32)) multiplexer_5 (
    .in0({32{1'b0}}), .in1(multiplexer_4_out), .out(multiplexer_5_out), .sel(register_2_q));
  and and_10 (stop_cache_D, BusyDa1, or_10_out);
  Register #(.width(14)) register_3 (.D(counter_1_q), .en(not_7_out), .clk(Clock), .Q(register_3_q), .clr(or_11_out));
  Register #(.width(32)) InstFetch (
    .D(multiplexer_5_out), .en(not_7_out), .clk(Clock),
    .Q({InstFetch_q_6, InstFetch_q_5, InstFetch_q_4, InstFetch_q_3, InstFetch_q_2, InstFetch_q}),
    .clr(or_11_out));
  not not_7 (not_7_out, stop_cache_D);
  or or_11 (or_11_out, Exception, branch_taken);
  Comparator #(.mode("unsigned"), .width(5)) comparator_1 (
    .a(Destino2_q), .b({5{1'b0}}), .gt(comparator_1_gt));  // open: eq, lt
  Comparator #(.width(7)) comparator_2 (.a(InstFetch_q), .b({7{1'b0}}), .eq(comparator_2_eq));  // open: gt, lt
  Comparator #(.mode("unsigned"), .width(5)) comparator_3 (
    .a(InstFetch_q_4), .b(Destino2_q), .eq(comparator_3_eq));  // open: gt, lt
  Comparator #(.mode("unsigned"), .width(5)) comparator_4 (
    .a(InstFetch_q_5), .b(Destino2_q), .eq(comparator_4_eq));  // open: gt, lt
  Translator translator_1 (
    .clock(Clock), .opCode(InstFetch_q), .funct3(InstFetch_q_3), .funct7(InstFetch_q_6),
    .TranslatedC(translator_1_translatedc));
  Register #(.width(14)) register_4 (
    .D(cache_datos_1_ram_address), .clk(and_8_out), .Q(register_4_q), .clr(or_13_out));  // open: en
  not not_8 (not_8_out, comparator_2_eq);
  Comparator #(.width(5)) comparator_5 (
    .a({5{1'b1}}), .b(translator_1_translatedc), .eq(comparator_5_eq));  // open: gt, lt
  Registros Registers (
    .writeEnable(Write), .exception(Exception), .clk(Clock), .writeDestiny(Destino), .nOp1(InstFetch_q_4),
    .nOp2(InstFetch_q_5), .writeData(WriteData), .op2(store_write_data), .op1(Registers_op1));
  and and_11 (and_11_out, comparator_3_eq, comparator_1_gt);
  and and_12 (and_12_out, comparator_4_eq, comparator_1_gt);
  Register #(.width(32)) register_5 (
    .D(cache_datos_1_ram_return_data), .clk(and_8_out), .Q(Data), .clr(or_13_out));  // open: en
  Register #(.width(1)) register_6 (
    .D(cache_datos_1_ram_write), .clk(and_8_out), .Q(ram_write_enable), .clr(or_13_out));  // open: en
  and and_13 (and_13_out, not_8_out, comparator_5_eq);
  Comparator #(.mode("unsigned"), .width(5)) comparator_6 (
    .a(Destino3_q), .b({5{1'b0}}), .gt(comparator_6_gt));  // open: eq, lt
  Multiplexer #(.width(14)) multiplexer_6 (
    .in0(register_4_q), .in1(cache_datos_1_ram_address), .out(addr_ram_in_d), .sel(load_enable));
  Multiplier #(.width(21)) multiplier_1 (
    .a({1'b0, InstFetch_q_6[6], InstFetch_q_4, InstFetch_q_3, InstFetch_q_5[0], InstFetch_q_6[5:0], InstFetch_q_5[4:1]}),
    .b(21'h2), .out(multiplier_1_out));  // open: cin, cout
  Multiplier #(.width(13)) multiplier_2 (
    .a({InstFetch_q_6[6], InstFetch_q_2[0], InstFetch_q_6[5:0], InstFetch_q_2[4:1], 1'b0}), .b(13'h2),
    .out(multiplier_2_out));  // open: cin, cout
  or or_12 (or_12_out, InvalidAddressExc, and_13_out);
  Comparator #(.mode("unsigned"), .width(5)) comparator_7 (
    .a(InstFetch_q_4), .b(Destino3_q), .eq(comparator_7_eq));  // open: gt, lt
  Comparator #(.mode("unsigned"), .width(5)) comparator_8 (
    .a(InstFetch_q_5), .b(Destino3_q), .eq(comparator_8_eq));  // open: gt, lt
  or or_13 (or_13_out, MissD, Exception);
  Register #(.width(1)) register_7 (.D(or_12_out), .en(or_12_out), .clk(Clock), .Q(Exception), .clr(manual_reset));
  and and_14 (and_14_out, comparator_7_eq, comparator_6_gt);
  and and_15 (and_15_out, comparator_8_eq, comparator_6_gt);
  Multiplexer #(.width(32)) multiplexer_7 (
    .in0({{20{1'b0}}, InstFetch_q_6, InstFetch_q_5}),
    .in1({InstFetch_q_6, InstFetch_q_5, InstFetch_q_4, InstFetch_q_3, {12{1'b0}}}), .out(multiplexer_7_out),
    .sel(or_14_out));
  or or_14 (or_14_out, comparator_9_eq, comparator_10_eq);
  Multiplexer #(.width(32)) multiplexer_8 (.in0(Registers_op1), .in1(NewPC), .out(multiplexer_8_out), .sel(and_11_out));
  Multiplexer #(.width(32)) multiplexer_9 (
    .in0(store_write_data), .in1(NewPC), .out(multiplexer_9_out), .sel(and_12_out));
  Comparator #(.width(5)) comparator_9 (
    .a(translator_1_translatedc), .b(5'b10010), .eq(comparator_9_eq));  // open: gt, lt
  Register #(.width(14)) register_8 (.D(register_3_q), .en(not_9_out), .clk(Clock), .Q(PC_Actual), .clr(Exception));
  Multiplexer #(.width(32)) multiplexer_10 (
    .in0(multiplexer_8_out), .in1(Resultado_q), .out(multiplexer_10_out), .sel(and_14_out));
  Multiplexer #(.width(32)) multiplexer_11 (
    .in0(multiplexer_9_out), .in1(Resultado_q), .out(multiplexer_11_out), .sel(and_15_out));
  Comparator #(.width(5)) comparator_10 (
    .a(translator_1_translatedc), .b(5'b10011), .eq(comparator_10_eq));  // open: gt, lt
  Register #(.width(12)) jalr_offset (
    .D({InstFetch_q_6, InstFetch_q_5}), .en(not_9_out), .clk(Clock), .Q(jalr_offset_q), .clr(Exception));
  Register #(.width(21)) register_9 (
    .D(multiplier_1_out), .en(not_9_out), .clk(Clock), .Q(register_9_q), .clr(Exception));
  Register #(.width(13)) branch_offset (
    .D(multiplier_2_out), .en(not_9_out), .clk(Clock), .Q(branch_offset_q), .clr(Exception));
  Register #(.width(32)) Instruction01 (
    .D({InstFetch_q_6, InstFetch_q_5, InstFetch_q_4, InstFetch_q_3, InstFetch_q_2, InstFetch_q}),
    .en(not_9_out), .clk(Clock), .Q({Instruction01_q[31:25], S_dest, Instruction01_q[19:0]}));  // open: clr
  Register #(.width(32)) store_offset_2 (
    .D({{20{1'b0}}, InstFetch_q_6, InstFetch_q_2}), .en(not_9_out), .clk(Clock), .Q(store_offset),
    .clr(Exception));
  Register #(.width(5)) OpCode2 (
    .D(translator_1_translatedc), .en(not_9_out), .clk(Clock), .Q(OpCode2_q), .clr(Exception));
  Register #(.width(5)) Destino2 (.D(InstFetch_q_2), .en(not_9_out), .clk(Clock), .Q(Destino2_q), .clr(Exception));
  Register #(.width(32)) Op1 (.D(multiplexer_10_out), .en(not_9_out), .clk(Clock), .Q(base_position), .clr(Exception));
  Register #(.width(32)) Op2 (.D(multiplexer_11_out), .en(not_9_out), .clk(Clock), .Q(Op2_q), .clr(Exception));
  Register #(.width(32)) Imm2 (.D(multiplexer_7_out), .en(not_9_out), .clk(Clock), .Q(load_offset), .clr(Exception));
  not not_9 (not_9_out, stop_cache_D);
  Comparator #(.mode("unsigned"), .width(5)) comparator_11 (
    .a(OpCode2_q), .b(5'b10011), .eq(RewritePC));  // open: gt, lt
  Multiplexer #(.width(32)) multiplexer_12 (
    .in0(base_position), .in1({{18{1'b0}}, PC_Actual}), .out(multiplexer_12_out), .sel(RewritePC));
  branch_jump branch_jump_1 (
    .opcode(OpCode2_q), .op1(base_position), .op2(Op2_q), .branch_offset(branch_offset_q),
    .jump_offset(register_9_q), .jalr_rs1(base_position), .jalr_offset(jalr_offset_q),
    .current_pc(PC_Actual), .rd_write_en(can_write_ra), .rd_data(return_address),
    .next_pc(branch_jump_1_next_pc), .branch_taken(branch_taken));
  assign ModifiedPC = {{18{branch_jump_1_next_pc[13]}}, branch_jump_1_next_pc};  // Bit_Extender bit_extender_1
  Comparator #(.width(5)) comparator_12 (.a(OpCode2_q), .b(5'b10100), .eq(SysCall));  // open: gt, lt
  Register #(.width(1)) register_10 (.D(branch_taken), .clk(Clock), .Q(bTaken));  // open: en, clr
  ALU ALU2 (.opCode(OpCode2_q), .op1(multiplexer_12_out), .op2(Op2_q), .imm(load_offset), .result(NewPC));
  Multiplexer #(.select(5), .width(32)) multiplexer_13 (
    .in0(NewPC), .in1(NewPC), .in2(NewPC), .in3(NewPC), .in4(NewPC), .in5(NewPC), .in6(NewPC), .in7(NewPC),
    .in8(NewPC), .in9(NewPC), .in10(NewPC), .in11(NewPC), .in12({32{1'b0}}), .in13({32{1'b0}}), .in14(NewPC),
    .in15(NewPC), .in16({32{1'b0}}), .in17({32{1'b0}}), .in18(NewPC), .in19({32{1'b0}}), .in20({32{1'b0}}),
    .in21({32{1'b0}}), .in22({32{1'b0}}), .in23({32{1'b0}}), .in24({32{1'b0}}), .in25({32{1'b0}}),
    .in26({32{1'b0}}), .in27({32{1'b0}}), .in28({32{1'b0}}), .in29({32{1'b0}}), .in30({32{1'b0}}),
    .in31({32{1'b0}}), .out(multiplexer_13_out), .sel(OpCode2_q));
  Register #(.width(32)) register_11 (
    .D(store_write_data), .en(not_10_out), .clk(Clock), .Q(register_11_q), .clr(Exception));
  addr_calculator addr_calculator_1 (
    .store_offset(store_offset), .load_offset(load_offset), .op_code_alu(OpCode2_q), .base(base_position),
    .addr(addr_calculator_1_addr));
  Register #(.width(32)) Instruction02 (
    .D({Instruction01_q[31:25], S_dest, Instruction01_q[19:0]}), .en(not_10_out), .clk(Clock));  // open: Q, clr
  Multiplexer #(.width(32)) multiplexer_14 (
    .in0(register_11_q), .in1(WriteData), .out(multiplexer_14_out), .sel(S_data_des));
  Register #(.width(14)) store_addr (
    .D(addr_calculator_1_addr), .en(not_10_out), .clk(Clock), .Q(addr_in), .clr(Exception));
  Register #(.width(5)) OpCode3 (.D(OpCode2_q), .en(not_10_out), .clk(Clock), .Q(OpCode3_q), .clr(Exception));
  Register #(.width(5)) Destino3 (.D(Destino2_q), .en(not_10_out), .clk(Clock), .Q(Destino3_q), .clr(Exception));
  Register #(.width(32)) Resultado (
    .D(multiplexer_13_out), .en(not_10_out), .clk(Clock), .Q(Resultado_q), .clr(Exception));
  Register #(.width(32)) return_address1 (
    .D(return_address), .en(not_10_out), .clk(Clock), .Q(return_address1_q), .clr(Exception));
  Register #(.width(1)) can_write_ra1 (
    .D(can_write_ra), .en(not_10_out), .clk(Clock), .Q(can_write_ra1_q), .clr(Exception));
  not not_10 (not_10_out, stop_cache_D);
  Register #(.width(32)) store_data (
    .D(multiplexer_14_out), .en(not_10_out), .clk(Clock), .Q(store_write_in), .clr(Exception));
  Register #(.width(5)) mem_OpCode (.D(OpCode3_q), .en(not_11_out), .clk(Clock), .Q(mem_OpCode_q), .clr(Exception));
  Register #(.width(5)) mem_Destino (.D(Destino3_q), .en(not_11_out), .clk(Clock), .Q(Destino), .clr(Exception));
  Register #(.width(32)) mem_Resultado (
    .D(Resultado_q), .en(not_11_out), .clk(Clock), .Q(mem_Resultado_q), .clr(Exception));
  Register #(.width(32)) return_address2 (
    .D(return_address1_q), .en(not_11_out), .clk(Clock), .Q(return_address2_q), .clr(Exception));
  Register #(.width(1)) can_write_ra2 (
    .D(can_write_ra1_q), .en(not_11_out), .clk(Clock), .Q(can_write_ra2_q), .clr(Exception));
  Decoder #(.select(5)) decoder_1 (
    .out12(load_enable), .out13(store_enable), .out14(decoder_1_out14), .out15(decoder_1_out15),
    .out20(decoder_1_out20), .sel(OpCode3_q));  // open: out0, out1, out2, out3, out4, out5, out6, out7, out8, out9, out10, out11, out16, out17, out18, out19, out21, out22, out23, out24, out25, out26, out27, out28, out29, out30, out31, en
  not not_11 (not_11_out, stop_cache_D);
  Multiplexer #(.width(32)) multiplexer_15 (
    .in0(mem_Resultado_q), .in1(load_result), .out(multiplexer_15_out), .sel(comparator_13_eq));
  Comparator #(.width(5)) comparator_13 (.a(mem_OpCode_q), .b(5'b01100), .eq(comparator_13_eq));  // open: gt, lt
  Comparator #(.mode("unsigned"), .width(5)) comparator_14 (
    .a(mem_OpCode_q), .b(5'b10100), .gt(comparator_14_gt));  // open: eq, lt
  or or_15 (or_15_out, decoder_1_out20, decoder_1_out15, decoder_1_out14, store_enable, comparator_14_gt);
  Multiplexer #(.width(32)) multiplexer_16 (
    .in0(multiplexer_15_out), .in1(return_address2_q), .out(WriteData), .sel(can_write_ra2_q));
  Decoder #(.select(5)) decoder_2 (
    .out12(decoder_2_out12), .out13(decoder_2_out13), .out14(decoder_2_out14), .out15(decoder_2_out15),
    .out20(decoder_2_out20), .sel(mem_OpCode_q));  // open: out0, out1, out2, out3, out4, out5, out6, out7, out8, out9, out10, out11, out16, out17, out18, out19, out21, out22, out23, out24, out25, out26, out27, out28, out29, out30, out31, en
  not not_12 (not_12_out, or_15_out);
  not not_13 (not_13_out, comparator_15_eq);
  Comparator #(.mode("unsigned"), .width(5)) comparator_15 (
    .a(mem_OpCode_q), .b({5{1'b0}}), .eq(comparator_15_eq));  // open: gt, lt
  Comparator #(.mode("unsigned"), .width(5)) comparator_16 (
    .a(Destino), .b(S_dest), .eq(comparator_16_eq));  // open: gt, lt
  or or_16 (or_16_out, decoder_2_out20, decoder_2_out15, decoder_2_out14, decoder_2_out13, decoder_2_out12);
  not not_14 (not_14_out, or_16_out);
  or or_17 (Write, not_14_out, not_12_out);
  and and_16 (S_data_des, not_12_out, not_13_out, comparator_16_eq);

  // Other names for the same wires on the sheet: ram_data_out[31:0] = Data; SystemCall = SysCall

  // Notes on the sheet:
  //   Cuando se activa indica que hay una syscall
  //   Cuando se activa indica que hay una excepcion
  //   Dependiendo de la instruccion, algo diferente tiene que salir
  //   Registro al que se escribira
  //   Este decoder nos dice si una instruccion escribe en registro
  //   Datos a escribir en registro
  //   Decide si debe escribirse algo en registro
endmodule

module Registros (
  input  [4:0] nOp1,
  input  [4:0] nOp2,
  input  [31:0] writeData,
  input  [4:0] writeDestiny,
  input  writeEnable,
  input  exception,
  input  clk,
  output [31:0] op1,
  output [31:0] op2
);

  wire and_1_out, decoder_1_out1, decoder_1_out2, decoder_1_out3, decoder_1_out4, decoder_1_out5,
       decoder_1_out6, decoder_1_out7, decoder_1_out8, decoder_1_out9, decoder_1_out10, decoder_1_out11,
       decoder_1_out12, decoder_1_out13, decoder_1_out14, decoder_1_out15, decoder_1_out16, decoder_1_out17,
       decoder_1_out18, decoder_1_out19, decoder_1_out20, decoder_1_out21, decoder_1_out22, decoder_1_out23,
       decoder_1_out24, decoder_1_out25, decoder_1_out26, decoder_1_out27, decoder_1_out28, decoder_1_out29,
       decoder_1_out30, decoder_1_out31, not_1_out, not_2_out;
  wire [4:0] multiplexer_1_out;
  wire [31:0] x0_q, x1_q, x2_q, x3_q, x4_q, x5_q, x6_q, x7_q, x8_q, x9_q, x10_q, x11_q, x12_q, x13_q, x14_q,
       x15_q, x16_q, x17_q, x18_q, x19_q, x20_q, x21_q, x22_q, x23_q, x24_q, x25_q, x26_q, x27_q, x28_q,
       x29_q, x30_q, x31_q;

  and and_1 (and_1_out, writeEnable, not_1_out);
  not not_1 (not_1_out, exception);
  not not_2 (not_2_out, and_1_out);
  Decoder #(.select(5)) decoder_1 (
    .out1(decoder_1_out1), .out2(decoder_1_out2), .out3(decoder_1_out3), .out4(decoder_1_out4),
    .out5(decoder_1_out5), .out6(decoder_1_out6), .out7(decoder_1_out7), .out8(decoder_1_out8),
    .out9(decoder_1_out9), .out10(decoder_1_out10), .out11(decoder_1_out11), .out12(decoder_1_out12),
    .out13(decoder_1_out13), .out14(decoder_1_out14), .out15(decoder_1_out15), .out16(decoder_1_out16),
    .out17(decoder_1_out17), .out18(decoder_1_out18), .out19(decoder_1_out19), .out20(decoder_1_out20),
    .out21(decoder_1_out21), .out22(decoder_1_out22), .out23(decoder_1_out23), .out24(decoder_1_out24),
    .out25(decoder_1_out25), .out26(decoder_1_out26), .out27(decoder_1_out27), .out28(decoder_1_out28),
    .out29(decoder_1_out29), .out30(decoder_1_out30), .out31(decoder_1_out31), .sel(multiplexer_1_out));  // open: out0, en
  Multiplexer #(.width(5)) multiplexer_1 (
    .in0(writeDestiny), .in1({5{1'b0}}), .out(multiplexer_1_out), .sel(not_2_out));
  Register #(.width(32)) x0 (.D(writeData), .Q(x0_q));  // open: en, clk, clr
  Register #(.width(32)) x1 (.D(writeData), .en(decoder_1_out1), .clk(clk), .Q(x1_q), .clr(exception));
  Register #(.width(32)) x2 (.D(writeData), .en(decoder_1_out2), .clk(clk), .Q(x2_q), .clr(exception));
  Register #(.width(32)) x3 (.D(writeData), .en(decoder_1_out3), .clk(clk), .Q(x3_q), .clr(exception));
  Register #(.width(32)) x4 (.D(writeData), .en(decoder_1_out4), .clk(clk), .Q(x4_q), .clr(exception));
  Register #(.width(32)) x5 (.D(writeData), .en(decoder_1_out5), .clk(clk), .Q(x5_q), .clr(exception));
  Register #(.width(32)) x6 (.D(writeData), .en(decoder_1_out6), .clk(clk), .Q(x6_q), .clr(exception));
  Register #(.width(32)) x7 (.D(writeData), .en(decoder_1_out7), .clk(clk), .Q(x7_q), .clr(exception));
  Register #(.width(32)) x8 (.D(writeData), .en(decoder_1_out8), .clk(clk), .Q(x8_q), .clr(exception));
  Register #(.width(32)) x9 (.D(writeData), .en(decoder_1_out9), .clk(clk), .Q(x9_q), .clr(exception));
  Register #(.width(32)) x10 (.D(writeData), .en(decoder_1_out10), .clk(clk), .Q(x10_q), .clr(exception));
  Register #(.width(32)) x11 (.D(writeData), .en(decoder_1_out11), .clk(clk), .Q(x11_q), .clr(exception));
  Register #(.width(32)) x12 (.D(writeData), .en(decoder_1_out12), .clk(clk), .Q(x12_q), .clr(exception));
  Register #(.width(32)) x13 (.D(writeData), .en(decoder_1_out13), .clk(clk), .Q(x13_q), .clr(exception));
  Register #(.width(32)) x14 (.D(writeData), .en(decoder_1_out14), .clk(clk), .Q(x14_q), .clr(exception));
  Register #(.width(32)) x15 (.D(writeData), .en(decoder_1_out15), .clk(clk), .Q(x15_q), .clr(exception));
  Multiplexer #(.select(5), .width(32)) multiplexer_2 (
    .in0(x0_q), .in1(x1_q), .in2(x2_q), .in3(x3_q), .in4(x4_q), .in5(x5_q), .in6(x6_q), .in7(x7_q),
    .in8(x8_q), .in9(x9_q), .in10(x10_q), .in11(x11_q), .in12(x12_q), .in13(x13_q), .in14(x14_q),
    .in15(x15_q), .in16(x16_q), .in17(x17_q), .in18(x18_q), .in19(x19_q), .in20(x20_q), .in21(x21_q),
    .in22(x22_q), .in23(x23_q), .in24(x24_q), .in25(x25_q), .in26(x26_q), .in27(x27_q), .in28(x28_q),
    .in29(x29_q), .in30(x30_q), .in31(x31_q), .out(op1), .sel(nOp1));
  Multiplexer #(.select(5), .width(32)) multiplexer_3 (
    .in0(x0_q), .in1(x1_q), .in2(x2_q), .in3(x3_q), .in4(x4_q), .in5(x5_q), .in6(x6_q), .in7(x7_q),
    .in8(x8_q), .in9(x9_q), .in10(x10_q), .in11(x11_q), .in12(x12_q), .in13(x13_q), .in14(x14_q),
    .in15(x15_q), .in16(x16_q), .in17(x17_q), .in18(x18_q), .in19(x19_q), .in20(x20_q), .in21(x21_q),
    .in22(x22_q), .in23(x23_q), .in24(x24_q), .in25(x25_q), .in26(x26_q), .in27(x27_q), .in28(x28_q),
    .in29(x29_q), .in30(x30_q), .in31(x31_q), .out(op2), .sel(nOp2));
  Register #(.width(32)) x16 (.D(writeData), .en(decoder_1_out16), .clk(clk), .Q(x16_q), .clr(exception));
  Register #(.width(32)) x17 (.D(writeData), .en(decoder_1_out17), .clk(clk), .Q(x17_q), .clr(exception));
  Register #(.width(32)) x18 (.D(writeData), .en(decoder_1_out18), .clk(clk), .Q(x18_q), .clr(exception));
  Register #(.width(32)) x19 (.D(writeData), .en(decoder_1_out19), .clk(clk), .Q(x19_q), .clr(exception));
  Register #(.width(32)) x20 (.D(writeData), .en(decoder_1_out20), .clk(clk), .Q(x20_q), .clr(exception));
  Register #(.width(32)) x21 (.D(writeData), .en(decoder_1_out21), .clk(clk), .Q(x21_q), .clr(exception));
  Register #(.width(32)) x22 (.D(writeData), .en(decoder_1_out22), .clk(clk), .Q(x22_q), .clr(exception));
  Register #(.width(32)) x23 (.D(writeData), .en(decoder_1_out23), .clk(clk), .Q(x23_q), .clr(exception));
  Register #(.width(32)) x24 (.D(writeData), .en(decoder_1_out24), .clk(clk), .Q(x24_q), .clr(exception));
  Register #(.width(32)) x25 (.D(writeData), .en(decoder_1_out25), .clk(clk), .Q(x25_q), .clr(exception));
  Register #(.width(32)) x26 (.D(writeData), .en(decoder_1_out26), .clk(clk), .Q(x26_q), .clr(exception));
  Register #(.width(32)) x27 (.D(writeData), .en(decoder_1_out27), .clk(clk), .Q(x27_q), .clr(exception));
  Register #(.width(32)) x28 (.D(writeData), .en(decoder_1_out28), .clk(clk), .Q(x28_q), .clr(exception));
  Register #(.width(32)) x29 (.D(writeData), .en(decoder_1_out29), .clk(clk), .Q(x29_q), .clr(exception));
  Register #(.width(32)) x30 (.D(writeData), .en(decoder_1_out30), .clk(clk), .Q(x30_q), .clr(exception));
  Register #(.width(32)) x31 (.D(writeData), .en(decoder_1_out31), .clk(clk), .Q(x31_q), .clr(exception));
endmodule

module addr_calculator (
  input  [31:0] store_offset,
  input  [31:0] load_offset,
  input  [4:0] op_code_alu,
  input  [31:0] base,
  output [13:0] addr
);

  wire comparator_1_eq;
  wire [31:0] multiplexer_1_out;
  wire [31:14] adder_1_out;

  Comparator #(.width(5)) comparator_1 (.a(op_code_alu), .b(5'b01100), .eq(comparator_1_eq));  // open: gt, lt
  Multiplexer #(.width(32)) multiplexer_1 (
    .in0(store_offset), .in1(load_offset), .out(multiplexer_1_out), .sel(comparator_1_eq));
  Adder #(.width(32)) adder_1 (.a(multiplexer_1_out), .b(base), .out({adder_1_out, addr}));  // open: cin, cout
endmodule

// VHDL entity ALU, as the project stores it:
LIBRARY ieee;
USE ieee.std_logic_1164.all;
USE ieee.numeric_std.all;

ENTITY ALU IS
  PORT (
    	opCode	: IN std_logic_vector(4 DOWNTO 0); -- codigo de operacion (5 bits)
	op1		: IN std_logic_vector(31 DOWNTO 0); -- operando 1 (32 bits)
	op2		: IN std_logic_vector(31 DOWNTO 0); -- operando 2 (32 bits)
    	imm		: IN std_logic_vector(31 DOWNTO 0); -- immediato (32 bits)
    	result   	: OUT std_logic_vector(31 DOWNTO 0)  -- resultado de la operacion (32 bits)
  );
END ALU;

--------------------------------------------------------------------------------
-- ALU Architecture Implementation
--------------------------------------------------------------------------------

ARCHITECTURE TypeArchitecture OF ALU IS
BEGIN
    PROCESS(opCode, op1, op2)
    BEGIN
        CASE opCode IS
            WHEN "00000" => -- ADD
                result <= std_logic_vector(signed(op1) + signed(op2));
            
            WHEN "00001" => -- SUB
                result <= std_logic_vector(signed(op1) - signed(op2));
            
            WHEN "00010" => -- ADDI
                result <= std_logic_vector(signed(op1) + signed(imm));
            
            WHEN "00011" => -- AND
                result <= op1 AND op2;
            
            WHEN "00100" => -- OR
                result <= op1 OR op2;
            
            WHEN "00101" => -- XOR
                result <= op1 XOR op2;
            
            WHEN "00110" => -- ANDI
                result <= op1 AND imm;
            
            WHEN "00111" => -- ORI
                result <= op1 OR imm;

            WHEN "01000" => -- XORI
                result <= op1 XOR imm;
            WHEN "01001" => -- SLL (Shift Left Logical)
	        	 result <= std_logic_vector(shift_left(unsigned(op1), to_integer(unsigned(op2(4 DOWNTO 0)))));
	
	       WHEN "01010" => -- SRL (Shift Right Logical)
	        	 result <= std_logic_vector(shift_right(unsigned(op1), to_integer(unsigned(op2(4 DOWNTO 0)))));
	
	       WHEN "01011" => -- SRA (Shift Right Arithmetic)
	        	 result <= std_logic_vector(shift_right(signed(op1), to_integer(unsigned(op2(4 DOWNTO 0)))));
	        
	       WHEN "10010" => -- LUI
	        	result <= imm(31 DOWNTO 12) & "000000000000";
	
	       WHEN "10011" => -- AUIPC
			  result <= std_logic_vector(
			    unsigned(op1) + unsigned(imm(31 downto 12) & "000000000000")
			  );
            WHEN OTHERS =>
                result <= (OTHERS => '0');
        END CASE;
    END PROCESS;

END TypeArchitecture;

// VHDL entity Translator, as the project stores it:
LIBRARY ieee;
USE ieee.std_logic_1164.all;

ENTITY Translator IS
  PORT (
  ------------------------------------------------------------------------------
  --Insert input ports below
  	clock     	: IN  std_logic; -- Clock usado para que el estado se actualice más seguido
    	opCode    	: IN  std_logic_vector(6 DOWNTO 0); -- Op Code que describe el tipo de instruccion
    	funct3	: IN  std_logic_vector(2 DOWNTO 0); -- funct3 que describe la instruccion especifica
    	funct7   	: IN  std_logic_vector(6 DOWNTO 0); -- funct7 que describe la instruccion especifica (solo en R-Type)
  ------------------------------------------------------------------------------
  --Insert output ports below
    TranslatedC	: OUT std_logic_vector(4 DOWNTO 0)  -- Codigo traducido
    );
END Translator;

--------------------------------------------------------------------------------
--Complete your VHDL description below
--------------------------------------------------------------------------------

ARCHITECTURE TypeArchitecture OF Translator IS

BEGIN
    PROCESS(opCode, funct3, funct7)
    BEGIN
        CASE opCode IS
       	WHEN "0110011" => -- R-Type
	       	-- ADD
	           IF funct3 = "000" and funct7 = "0000000" THEN
	           	TranslatedC <= "00000"; 
	           END IF;
	           -- SUB
	           IF funct3 = "000" and funct7 = "0100000" THEN
	           	TranslatedC <= "00001"; 
	           END IF;
	           -- AND
	           IF funct3 = "010" and funct7 = "0000000" THEN
	           	TranslatedC <= "00011"; 
	           END IF;
	           -- OR
	           IF funct3 = "100" and funct7 = "0000000" THEN
	           	TranslatedC <= "00100"; 
	           END IF;
	           -- XOR
	           IF funct3 = "110" and funct7 = "0000000" THEN
	           	TranslatedC <= "00101"; 
	           END IF;
	           -- 	SLL
	           IF funct3 = "001" and funct7 = "0000000" THEN
	           	TranslatedC <= "01001"; 
	           END IF;
	           --	SRL
	           IF funct3 = "101" and funct7 = "0000000" THEN
	           	TranslatedC <= "01010"; 
	           END IF;
	           --	SRA
	           IF funct3 = "101" and funct7 = "0100000" THEN
	           	TranslatedC <= "01011"; 
	           END IF;
		WHEN "0010011" => -- I-Type
			-- ADDi
	           IF funct3 = "000" THEN
	           	TranslatedC <= "00010"; 
	           END IF;
	           -- ANDi
	           IF funct3 = "010" THEN
	           	TranslatedC <= "00110"; 
	           END IF;
	           -- ORi
	           IF funct3 = "100" THEN
	           	TranslatedC <= "00111"; 
	           END IF;
	           -- XORi
	           IF funct3 = "110" THEN
	           	TranslatedC <= "01000"; 
	           END IF;
		WHEN "1100011" => -- B-Type
		  	-- BEQ
	         	IF funct3 = "000" THEN
          			TranslatedC <= "01110"; 
	         	END IF;
	          -- BNE
	          	IF funct3 = "001" THEN
	          		TranslatedC <= "01111"; 
	      	END IF;
                
      	WHEN "1101111" => -- jal
           	IF funct3 = "000" THEN
               		TranslatedC <= "10000"; 
              	END IF;
        	WHEN "1100111" => -- jalr
               	IF funct3 = "000" THEN
                	TranslatedC <= "10001"; 
               	END IF;
                
        	WHEN "0110111" => -- U-Type
            	-- 	LUI
              	
               	TranslatedC <= "10010"; 
             	
        	WHEN "0010111" => -- U-Type 2
           	-- 	AUIPC
              	
               TranslatedC <= "10011"; 
              	
 
        	WHEN "1110011" => -- I-Type 2
			-- 	ECALL
              	
               TranslatedC <= "10100"; 
              	
        	WHEN "0000011" => -- Load
           	IF funct3 = "010" THEN -- sw
               		TranslatedC <= "01100"; 
              	END IF;
        	WHEN "0100011" => -- S-Type
           	IF funct3 = "010" THEN -- sw
				TranslatedC <= "01101"; 
              	END IF;
         	WHEN "0000000" => -- Empty
			IF funct3 = "000" and funct7 = "0000000" THEN
				TranslatedC <= "00000";
			END IF;
       	WHEN OTHERS =>
           	TranslatedC <= "11111";
        END CASE;
    END PROCESS;

END TypeArchitecture;

// VHDL entity branch_jump, as the project stores it:
library IEEE;
use IEEE.STD_LOGIC_1164.ALL;
use IEEE.NUMERIC_STD.ALL;

entity branch_jump is
    port (
        opcode        : in  std_logic_vector(4 downto 0); -- codigo de operacion
        op1           : in  std_logic_vector(31 downto 0); -- operando 1 para branches
        op2           : in  std_logic_vector(31 downto 0); -- operando 2 para branches
        branch_offset : in  std_logic_vector(12 downto 0); -- offset para branches
        jump_offset   : in  std_logic_vector(20 downto 0); -- offset para jal
        jalr_rs1      : in  std_logic_vector(31 downto 0); -- valor del registro para calcular el offset de jalr
        jalr_offset   : in  std_logic_vector(11 downto 0); -- offset para jalr
        current_pc    : in  std_logic_vector(13 downto 0); -- PC actual
        rd_write_en   : out std_logic;                      -- booleano para saber si se va a escribir en el registro destino de los jumps o no
        rd_data       : out std_logic_vector(31 downto 0); -- data a escribir en el registro destino de los jumps
        next_pc       : out std_logic_vector(13 downto 0); -- PC con el offset sumado
        branch_taken  : out std_logic 					-- booleano para saber si se va a hacer o no el branch
    );
end branch_jump;

architecture Behavioral of branch_jump is

	-- constantes definidas segun los 4 tipos de OP codes que se pueden recibir
    constant OP_BEQ  : std_logic_vector(4 downto 0) := "01110"; -- beq
    constant OP_BNE  : std_logic_vector(4 downto 0) := "01111"; -- bne
    constant OP_JAL  : std_logic_vector(4 downto 0) := "10000"; -- jal
    constant OP_JALR : std_logic_vector(4 downto 0) := "10001"; -- jalr

    -- booleanos para identificar que operacion se esta realizando
    signal is_beq, is_bne, is_jal, is_jalr : std_logic;

    -- booleanos para saber si tomar o no el branch
    signal branch_eq, take_branch          : std_logic;

    -- aqui se guardan los offsets ajustados segun el numero de bits para que sea el mismo que el PC
    signal branch_off_ext : std_logic_vector(13 downto 0); 
    signal jump_off_ext   : std_logic_vector(13 downto 0); 
    signal jalr_off_ext   : std_logic_vector(13 downto 0); 

    -- aqui se guarda el retorno de los jumps, que seria la instruccion siguiente del jump
    signal pc_plus_one    : std_logic_vector(13 downto 0);
    
begin

    -- definir los booleanos de tipo de operacion segun el OP code
    is_beq  <= '1' when opcode = OP_BEQ  else '0';
    is_bne  <= '1' when opcode = OP_BNE  else '0';
    is_jal  <= '1' when opcode = OP_JAL  else '0';
    is_jalr <= '1' when opcode = OP_JALR else '0';

    -- se revisa si los operandos son iguales, si lo son se activa este booleano
    branch_eq <= '1' when op1 = op2 else '0';
    
    -- se revisa si la operacion que estamos haciendo es un branch, si lo es entonces se revisa si se cumple el beq o bne y de ser asi se activa este booleano
    take_branch <= (is_beq and branch_eq) or (is_bne and (not branch_eq));

    -- se toman los offsets y se ajusta su cantidad de bits
    branch_off_ext <= std_logic_vector(resize(signed(branch_offset), 14));
    jump_off_ext   <= std_logic_vector(resize(signed(jump_offset), 14));
    jalr_off_ext   <= std_logic_vector(resize(signed(jalr_offset), 14));

    -- se calcula el retorno de los jumps sumandole 1 al PC actual
    pc_plus_one <= std_logic_vector(unsigned(current_pc) + 1);

    -- este proceso se activa cada vez que alguna de estas variables se modifica
    process(opcode, op1, op2, branch_off_ext, jump_off_ext, jalr_off_ext,
            current_pc, take_branch, is_jal, is_jalr, pc_plus_one, jalr_rs1)
            
        -- esta variable se usa para guardar el offset completo del jalr (offset + valor del registro)
        variable complete_offset : unsigned(31 downto 0);
        
    begin
    
    	   -- inicializar variables
        rd_write_en <= '0';
        rd_data <= (others => '0');
        next_pc <= pc_plus_one;
        branch_taken <= '0';

        -- si la operacion es un branch y se sabe que si se va a hacer el branch:
        if take_branch = '1' then
        	  -- calcular nuevo PC sumandole al actual el offset
            next_pc <= std_logic_vector(unsigned(current_pc) + unsigned(branch_off_ext));
            -- activar booleano para saber en el circuito que si se tomo el branch
            branch_taken <= '1';
        -- si la operacion es un jal:
        elsif is_jal = '1' then
        	  -- se activa el booleano para saber en el circuito que se puede escribir en el registro destino
            rd_write_en <= '1';
            -- guardar en esta variable de retorno el dato a escribir en el registro destino (el retorno del jump)
            rd_data <= std_logic_vector(resize(unsigned(pc_plus_one), 32));
            -- calcular nuevo PC sumandole el offset del jal
            next_pc <= std_logic_vector(unsigned(current_pc) + unsigned(jump_off_ext));
            -- activar booleano para saber en el circuito que si se va a hacer el jump
            branch_taken <= '1';

        elsif is_jalr = '1' then
            -- se activa el booleano para saber en el circuito que se puede escribir en el registro destino
            rd_write_en <= '1';
            -- guardar en esta variable de retorno el dato a escribir en el registro destino (el retorno del jump)
            rd_data <= std_logic_vector(resize(unsigned(pc_plus_one), 32));
            -- se calcula el offset completo sumandole al offset el valor del registro
            complete_offset := unsigned(jalr_rs1) + unsigned(jalr_off_ext);
            -- calcular nuevo PC sumandole el offset completo del jalr
            next_pc <= std_logic_vector(complete_offset(13 downto 0));
            -- activar booleano para saber en el circuito que si se va a hacer el jump
            branch_taken <= '1';
        end if;
    end process;

end Behavioral;

// VHDL entity cache_datos, as the project stores it:
library IEEE;
use IEEE.STD_LOGIC_1164.ALL;
use IEEE.NUMERIC_STD.ALL;
use STD.TEXTIO.ALL;
use IEEE.STD_LOGIC_TEXTIO.ALL;

entity cache_datos is
  Port (
      clk         : in  STD_LOGIC;
      reset       : in  STD_LOGIC;
      cpu_asked_address    : in  STD_LOGIC_VECTOR(13 downto 0); -- direccion pedida por la cpu
      cpu_data_to_write : in  STD_LOGIC_VECTOR(31 downto 0); -- dato que se quiere escribir en memoria
      cpu_return_data: out STD_LOGIC_VECTOR(31 downto 0); -- dato leido desde la cache
      cpu_write   : in  STD_LOGIC; -- señal que indica que se quiere escribir en memoria
      cpu_read    : in  STD_LOGIC; -- señal que indica que se quiere leer de memoria
      cpu_enable  : in  STD_LOGIC; -- señal que habilita las operaciones de memoria
    
      ram_address    : out STD_LOGIC_VECTOR(13 downto 0); -- direccion de memoria a leer o a escribir en la ram
      ram_data_to_write : in  STD_LOGIC_VECTOR(31 downto 0); -- dato a escribir en la ram
      ram_return_data: out STD_LOGIC_VECTOR(31 downto 0); -- dato extraido de la ram tras una lectura
      ram_write   : out STD_LOGIC; -- señal que indica que se quiere escribir en la ram
      ram_read    : out STD_LOGIC; -- señal que indica que se quiere leer de la ram
    
      cache_hit   : out STD_LOGIC; -- señal que indica un hit
      cache_miss  : out STD_LOGIC; -- señal que indica un miss
      busy        : out STD_LOGIC; -- señal que indica que la cache esta ocupada
    
      monitor_enable : in STD_LOGIC -- para imprimir cosas
  );
end cache_datos;

architecture Behavioral of cache_datos is

  -- constantes que indican la organizacion de la cache
  constant CACHE_SIZE    : integer := 32; -- 32 bloques
  constant BLOCK_SIZE    : integer := 4; -- 4 palabras por bloque
  constant WORD_SIZE     : integer := 32; -- palabras de 32 bits
  constant INDEX_BITS    : integer := 5; -- 5 bits de indice
  constant OFFSET_BITS   : integer := 2; -- 2 bits de offset
  constant TAG_BITS      : integer := 7; -- 7 bits de tag

  -- estructura de los bloques de cache: tiene un valid bit, un dirty bit, un tag y 4 palabras
  type word_array is array (0 to BLOCK_SIZE-1) of STD_LOGIC_VECTOR(WORD_SIZE-1 downto 0);
  type cache_block is record
      valid : STD_LOGIC;
      dirty : STD_LOGIC;
      tag   : STD_LOGIC_VECTOR(TAG_BITS-1 downto 0);
      data  : word_array;
  end record;
  type cache_array is array (0 to CACHE_SIZE-1) of cache_block;

  -- la cache se trata como una maquina de estados, estos son sus posibles estados:
  -- idle: espera a que la cpu habilite una operacion
  -- check_hit: revisa si hay hit
  -- read_miss: lee un bloque desde la ram
  -- write_back: escribe un bloque sucio en la ram antes de escribir
  -- allocate: carga un bloque a cache
  -- write_through: escribe en cache y en la ram
  type state_type is (IDLE, CHECK_HIT, READ_MISS, WRITE_BACK, ALLOCATE, WRITE_THROUGH);

  -- señales internas
  signal cache_mem : cache_array;
  signal current_state, next_state : state_type;

  -- asi se decodifica la direccion:
  signal addr_tag    : STD_LOGIC_VECTOR(TAG_BITS-1 downto 0); -- tag de la direccion
  signal addr_index  : STD_LOGIC_VECTOR(INDEX_BITS-1 downto 0); -- indice de la direccion
  signal addr_offset : STD_LOGIC_VECTOR(OFFSET_BITS-1 downto 0); -- offset de la direccion

  signal hit_detected : STD_LOGIC; -- señal que indica que hubo un hit
  signal miss_detected : STD_LOGIC; -- señal que indica que hubo un miss
  signal current_block : cache_block; -- bloque actual
  signal index_int : integer range 0 to CACHE_SIZE-1; -- indice para identificar el bloque de cache a acceder
  signal offset_int : integer range 0 to BLOCK_SIZE-1; -- indice para identificar la palabra dentro de ese bloque a acceder

  -- contador para operaciones de bloque
  -- se extiende en 3 para dar tiempo a la última palabra (3 ciclos de retraso)
  signal word_counter : integer range 0 to BLOCK_SIZE + 3;

  signal read_data_buffer : word_array; -- buffer en donde se concatenan las 4 palabras de la ram para enviarlas a la cache
  signal data_valid_flag : STD_LOGIC;  -- señal que indica si los datos son validos
  signal ram_read_internal : STD_LOGIC; -- señal para controlar lecturas en la ram
  signal previous_ram_read : STD_LOGIC; -- guarda el valor anterior de ram_read_internal

  -- convertir std_logic_vector a string para despues imprimirlo (debuggeo)
  function slv_to_string(slv : STD_LOGIC_VECTOR) return string is
      variable result : string(1 to slv'length);
      variable r : integer := 1;
  begin
      for i in slv'range loop
          if slv(i) = '1' then
              result(r) := '1';
          else
              result(r) := '0';
          end if;
          r := r + 1;
      end loop;
      return result;
  end function;

begin

  -- decodificar la direccion segun el esquema anterior
  addr_tag    <= cpu_asked_address(13 downto 7);
  addr_index  <= cpu_asked_address(6 downto 2);
  addr_offset <= cpu_asked_address(1 downto 0);
  index_int <= to_integer(unsigned(addr_index));
  offset_int <= to_integer(unsigned(addr_offset));
  current_block <= cache_mem(index_int);

  -- detectar hits y misses
  hit_detected <= '1' when (current_block.valid = '1' and -- hay hit si el bloque actual es valido y si el tag del bloque actual es igual al tag de la direccion
                           current_block.tag = addr_tag) else '0';
  miss_detected <= not hit_detected; -- hay miss en caso contrario

  -- se activan algunas salidas
  cache_hit <= hit_detected when current_state = CHECK_HIT else '0'; -- se retorna que hubo hit en caso de haberlo
  cache_miss <= miss_detected when current_state = CHECK_HIT else '0'; -- se retorna miss en caso de haberlo
  busy <= '1' when current_state /= IDLE else '0'; -- se detecta busy si el estado no es IDLE
  ram_read <= ram_read_internal;

  -- proceso que establece como se haran los cambios de estado y la logica del contador de operaciones de bloque
  process(clk, reset)
  begin
         -- si la señal reset esta activada entonces todo se reinicia y el estado pasa a IDLE
      if reset = '1' then
          current_state <= IDLE;
          word_counter <= 0;
          previous_ram_read <= '0';
      -- si no hay reset, con cada relojazo cambia el estado
      elsif rising_edge(clk) then
          current_state <= next_state;
          previous_ram_read <= ram_read_internal;
        
          -- logica del contador de operaciones de bloque
          if current_state = READ_MISS or current_state = WRITE_BACK then
              if (current_state = READ_MISS and word_counter < BLOCK_SIZE + 2) or
                 (current_state = WRITE_BACK and word_counter < BLOCK_SIZE) then
                  word_counter <= word_counter + 1;
              else
                  word_counter <= 0;
              end if;
          else
              word_counter <= 0;
          end if;
      end if;
  end process;

  -- proceso que se encarga de los cambios entre estados
  process(current_state, cpu_enable, cpu_read, cpu_write, hit_detected,
          miss_detected, word_counter, current_block.dirty)
  begin
      case current_state is
            -- si el estado actual es IDLE, solo pasa a CHECK_HIT si la señal de leer o escribir en memoria esta activada
          when IDLE =>
              if cpu_enable = '1' and (cpu_read = '1' or cpu_write = '1') then
                  next_state <= CHECK_HIT;
              else
                  next_state <= IDLE;
              end if;
          -- si el estado es CHECK_HIT pasa a WRITE_THOUGH si hay un hit y esta activada la señal de escritura en memoria y pasa a IDLE en caso contrario
          -- para a WRITE_BACK si hay un miss y el bloque actual es valido y su dirty bit es 1, y pasa a read_MISS en caso contrario
          -- en cualquier otro caso para a IDLE
          when CHECK_HIT =>
              if hit_detected = '1' then
                  if cpu_write = '1' then
                      next_state <= WRITE_THROUGH;
                  else
                      next_state <= IDLE;
                  end if;
              elsif miss_detected = '1' then
                  if current_block.valid = '1' and current_block.dirty = '1' then
                      next_state <= WRITE_BACK;
                  else
                      next_state <= READ_MISS;
                  end if;
              else
                  next_state <= IDLE;
              end if;
          -- si el estado actual es WRITE_BACK pasa a read_MISS si el contador de operaciones de bloque es mayor o igual al tamaño del bloque, y se mantiene en WRITE_BACK en caso contrario
          when WRITE_BACK =>
              if word_counter >= BLOCK_SIZE then
                  next_state <= READ_MISS;
              else
                  next_state <= WRITE_BACK;
              end if;
          -- si el estado actual es READ_MISS pasa a ALLOCATE si el contador de operaciones de bloque es mayor o igual al tamaño del bloque + 2, y se mantiene en READ_MISS en caso contrario
          when READ_MISS =>
              if word_counter >= BLOCK_SIZE + 2 then
                  next_state <= ALLOCATE;
              else
                  next_state <= READ_MISS;
              end if;
          -- si el estado actual es ALLOCATE pasa a WRITE_THROUGH si esta activada la señal de escritura en memoria, pasa a IDLE en caso contrario
          when ALLOCATE =>
              if cpu_write = '1' then
                  next_state <= WRITE_THROUGH;
              else
                  next_state <= IDLE;
              end if;
          -- de WRITE_THROUH se pasa a IDLE incondicionalemente
          when WRITE_THROUGH =>
              next_state <= IDLE;
          -- el estado por defecto es IDLE
          when others =>
              next_state <= IDLE;
      end case;
  end process;

  -- proceso que se encarga de la logica de cada estado
  process(clk, reset)
      variable temp_block : cache_block;
      variable line : line;
  begin
      if reset = '1' then
          -- Inicializar todos los datos
          for i in 0 to CACHE_SIZE-1 loop
              cache_mem(i).valid <= '0';
              cache_mem(i).dirty <= '0';
              cache_mem(i).tag <= (others => '0');
              for j in 0 to BLOCK_SIZE-1 loop
                  cache_mem(i).data(j) <= (others => '0');
              end loop;
          end loop;
        
          for j in 0 to BLOCK_SIZE-1 loop
              read_data_buffer(j) <= (others => '0');
          end loop;
        
          ram_address <= (others => '0');
          ram_return_data <= (others => '0');
          ram_write <= '0';
          ram_read_internal <= '0';
          cpu_return_data <= (others => '0');
          data_valid_flag <= '0';
        
      elsif rising_edge(clk) then
        
          -- Inicializar todas las salidas a 0 al inicio de cada ciclo
          ram_write <= '0';
          ram_read_internal <= '0';
          data_valid_flag <= '0';
          ram_address <= (others => '0');
          ram_return_data <= (others => '0');
          cpu_return_data <= (others => '0');
        
          case current_state is
               -- logica del estado IDLE
              when IDLE =>
                  -- no pasa nada
                  ram_address <= (others => '0');
                  ram_return_data <= (others => '0');
              -- logica del estado CHECK_HIT
              when CHECK_HIT =>
                  -- si hay hit y esta activada la bandera de lectura de memoria se devuelve el dato que indique el indice
                  if hit_detected = '1' and cpu_read = '1' then
                      cpu_return_data <= current_block.data(offset_int);
                      -- prints
                      if monitor_enable = '1' then
                          write(line, string'("Estado CHECK_HIT, direccion "));
                          write(line, slv_to_string(cpu_asked_address));
                          write(line, string'(" dato: "));
                          write(line, slv_to_string(current_block.data(offset_int)));
                          writeline(output, line);
                      end if;
                  end if;
              -- logica del estado WRITE_BACK
              when WRITE_BACK =>
                  -- escribe las 4 palabras en la ram
                  if word_counter < BLOCK_SIZE then
                      ram_address <= current_block.tag & addr_index & std_logic_vector(to_unsigned(word_counter, 2));
                      ram_return_data <= current_block.data(word_counter);
                      ram_write <= '1';
                  end if;
                
                  if monitor_enable = '1' and word_counter = 0 then
                      write(line, string'("Estado WRITE-BACK: Bloque "));
                      write(line, index_int);
                      writeline(output, line);
                  end if;
              -- logica del estado READ_MISS
              when READ_MISS =>
                  if word_counter < BLOCK_SIZE then
                      -- se piden las 4 palabras a la ram
                      ram_address <= addr_tag & addr_index & std_logic_vector(to_unsigned(word_counter, 2));
                      ram_read_internal <= '1';
                      -- prints
                      if monitor_enable = '1' then
                          write(line, string'("Estado READ_MISS, pidiendo palabra "));
                          write(line, word_counter);
                          write(line, string'(" direccion "));
                          write(line, slv_to_string(addr_tag & addr_index & std_logic_vector(to_unsigned(word_counter, 2))));
                          writeline(output, line);
                      end if;
                  end if;

                  -- traer datos con 3 ciclos de retraso
                  -- la ram tarda 3 ciclos en traer los datos, entonces por eso hay un retraso
                  if word_counter >= 3 and word_counter <= BLOCK_SIZE + 2 then
                      read_data_buffer(word_counter - 3) <= ram_data_to_write;
                      data_valid_flag <= '1';
                      -- prints
                      if monitor_enable = '1' then
                          write(line, string'("Almacenando indice"));
                          write(line, word_counter - 3);
                          write(line, string'(" dato "));
                          write(line, slv_to_string(ram_data_to_write));
                          writeline(output, line);
                      end if;
                  end if;
                  -- prints
                  if monitor_enable = '1' and word_counter = 0 then
                      write(line, string'("Leyendo bloque "));
                      write(line, index_int);
                      write(line, string'(" Tag "));
                      write(line, slv_to_string(addr_tag));
                      writeline(output, line);
                  end if;
              -- logica del estado ALLOCATE
              when ALLOCATE =>
                  -- se carga lo que haya en el buffer en el bloque de la cache correspondiente
                  temp_block := cache_mem(index_int);
                  temp_block.data := read_data_buffer;
                  -- se actualizan los valid, dirty y tag bit
                  temp_block.valid := '1';
                  temp_block.dirty := '0';
                  temp_block.tag := addr_tag;
                  cache_mem(index_int) <= temp_block;
                
                  -- si la señal de lectura de memoria estaba activada entonces se retorna ese valor
                  if cpu_read = '1' then
                      cpu_return_data <= read_data_buffer(offset_int);
                  end if;
                  -- prints
                  if monitor_enable = '1' then
                      write(line, string'("Estado ALLOCATE, bloque "));
                      write(line, index_int);
                      write(line, string'(" Tag "));
                      write(line, slv_to_string(addr_tag));
                      write(line, string'(" Palabra1"));
                      write(line, slv_to_string(read_data_buffer(0)));
                      write(line, string'(" Palabra2"));
                      write(line, slv_to_string(read_data_buffer(1)));
                      write(line, string'(" Palabra3"));
                      write(line, slv_to_string(read_data_buffer(2)));
                      write(line, string'(" Palabra4"));
                      write(line, slv_to_string(read_data_buffer(3)));
                      writeline(output, line);
                  end if;
              -- logica del estado WRITE_THROUGH
              when WRITE_THROUGH =>
                  -- se escribe en cache
                  temp_block := cache_mem(index_int);
                  temp_block.data(offset_int) := cpu_data_to_write;
                  temp_block.dirty := '1';
                  cache_mem(index_int) <= temp_block;
                
                  -- se escribe en ram
                  ram_address <= cpu_asked_address;
                  ram_return_data <= cpu_data_to_write;
                  ram_write <= '1';
                  -- prints
                  if monitor_enable = '1' then
                      write(line, string'("Estado WRITE_THROUGH, direccion "));
                      write(line, slv_to_string(cpu_asked_address));
                      write(line, string'(" Dato "));
                      write(line, slv_to_string(cpu_data_to_write));
                      writeline(output, line);
                  end if;
                
              when others =>
                  ram_address <= (others => '0');
                  ram_return_data <= (others => '0');
                  cpu_return_data <= (others => '0');
          end case;
      end if;
  end process;

end Behavioral;

// VHDL entity cache_instrucciones, as the project stores it:
library IEEE;
use IEEE.STD_LOGIC_1164.ALL;
use IEEE.NUMERIC_STD.ALL;
use STD.TEXTIO.ALL;
use IEEE.STD_LOGIC_TEXTIO.ALL;

entity cache_instrucciones is
 Port (
     clk         : in  STD_LOGIC;
     reset       : in  STD_LOGIC;
  
     cpu_address    : in  STD_LOGIC_VECTOR(13 downto 0); -- direccion solicitada
     cpu_instruction : out STD_LOGIC_VECTOR(31 downto 0); -- instruccion leida de la cache
     cpu_read    : in  STD_LOGIC; -- señal que indica que se quiere leer de memoria
     cpu_enable  : in  STD_LOGIC; -- señal que habilita las operaciones de memoria
  
     ram_address    : out STD_LOGIC_VECTOR(13 downto 0); -- direccion de memoria a leer o a escribir en la ram
     ram_data_to_write : in  STD_LOGIC_VECTOR(31 downto 0); -- dato a escribir en la ram
     ram_read    : out STD_LOGIC; -- señal que indica que se quiere leer de la ram
  
     cache_hit   : out STD_LOGIC; -- señal que indica un hit
     cache_miss  : out STD_LOGIC; -- señal que indica un miss
     busy        : out STD_LOGIC; -- señal que indica que la cache esta ocupada
  
     monitor_enable : in STD_LOGIC -- para prints
 );
end cache_instrucciones;

architecture Behavioral of cache_instrucciones is

-- constantes que indican la organizacion de la cache
 constant CACHE_SIZE    : integer := 16; -- 16 bloques
 constant BLOCK_SIZE    : integer := 8; -- 8 palabras por bloque
 constant WORD_SIZE     : integer := 32; -- palabras de 32 bits
 constant INDEX_BITS    : integer := 4; -- 4 bits de indice
 constant OFFSET_BITS   : integer := 3; -- 3 bits de offset
 constant TAG_BITS      : integer := 7; -- 7 bits de tag

 -- estructura de los bloques de cache: tiene un valid bit, un dirty bit, un tag y 4 palabras
 type word_array is array (0 to BLOCK_SIZE-1) of STD_LOGIC_VECTOR(WORD_SIZE-1 downto 0);
 type cache_block is record
     valid : STD_LOGIC;
     tag   : STD_LOGIC_VECTOR(TAG_BITS-1 downto 0);
     data  : word_array;
 end record;
 type cache_array is array (0 to CACHE_SIZE-1) of cache_block;

 -- la cache se trata como una maquina de estados, estos son sus posibles estados:
 -- idle: espera a que la cpu habilite una operacion
 -- check_hit: revisa si hay hit
 -- read_miss: lee un bloque desde la ram
 -- allocate: carga un bloque a cache
 type state_type is (IDLE, CHECK_HIT, READ_MISS, ALLOCATE);

 -- señales internas
 signal cache_mem : cache_array;
 signal current_state, next_state : state_type;

 -- asi se decodifica la direccion:
 signal addr_tag    : STD_LOGIC_VECTOR(TAG_BITS-1 downto 0); -- tag de la direccion
 signal addr_index  : STD_LOGIC_VECTOR(INDEX_BITS-1 downto 0); -- indice de la direccion
 signal addr_offset : STD_LOGIC_VECTOR(OFFSET_BITS-1 downto 0); -- offset de la direccion

 signal hit_detected : STD_LOGIC; -- señal que indica que hubo un hit
 signal miss_detected : STD_LOGIC; -- señal que indica que hubo un miss
 signal current_block : cache_block; -- bloque actual
 signal index_int : integer range 0 to CACHE_SIZE-1; -- indice para identificar el bloque de cache a acceder
 signal offset_int : integer range 0 to BLOCK_SIZE-1; -- indice para identificar la palabra dentro de ese bloque a acceder

 -- se usa para calcular la direccion de inicio del bloque de 8 palabras para acceder de forma secuencial a ellas
 signal block_initial_addr: STD_LOGIC_VECTOR(13 downto 0);

 -- contador para operaciones de bloque
 -- se extiende en 2 para dar tiempo a la última palabra
 signal word_counter : integer range 0 to BLOCK_SIZE + 2;

 -- Buffer temporal para lectura
 signal read_data_buffer : word_array; -- buffer en donde se concatenan las 8 palabras de la ram para enviarlas a la cache
 signal ram_read_internal : STD_LOGIC; -- señal para controlar lecturas en la ram

 -- convertir std_logic_vector a string para despues imprimirlo (debuggeo)
 function slv_to_string(slv : STD_LOGIC_VECTOR) return string is
     variable result : string(1 to slv'length);
     variable r : integer := 1;
 begin
     for i in slv'range loop
         if slv(i) = '1' then
             result(r) := '1';
         else
             result(r) := '0';
         end if;
         r := r + 1;
     end loop;
     return result;
 end function;

begin

-- decodificar la direccion segun el esquema anterior
 addr_tag    <= cpu_address(13 downto 7);
 addr_index  <= cpu_address(6 downto 3);
 addr_offset <= cpu_address(2 downto 0);
 index_int <= to_integer(unsigned(addr_index));
 offset_int <= to_integer(unsigned(addr_offset));
 current_block <= cache_mem(index_int);

 -- calcular la direccion de inicio del bloque
 block_initial_addr<= addr_tag & addr_index & "000";

-- detectar hits y misses
 hit_detected <= '1' when (current_block.valid = '1' and -- hay hit si el bloque actual es valido y si el tag del bloque actual es igual al tag de la direccion
                          current_block.tag = addr_tag) else '0';
 miss_detected <= not hit_detected; -- hay miss en caso contrario

-- se activan algunas salidas
 cache_hit <= hit_detected when current_state = CHECK_HIT else '0'; -- se retorna que hubo hit en caso de haberlo
 cache_miss <= miss_detected when current_state = CHECK_HIT else '0'; -- se retorna miss en caso de haberlo
 busy <= '1' when current_state /= IDLE else '0'; -- se detecta busy si el estado no es IDLE
 ram_read <= ram_read_internal;

-- proceso que establece como se haran los cambios de estado y la logica del contador de operaciones de bloque
 process(clk, reset)
 begin
      -- si la señal reset esta activada entonces todo se reinicia y el estado pasa a IDLE
     if reset = '1' then
         current_state <= IDLE;
         word_counter <= 0;
    -- si no hay reset, con cada relojazo cambia el estado
     elsif rising_edge(clk) then
         current_state <= next_state;
      
        -- logica del contador de operaciones de bloque
         if current_state = READ_MISS then
             if word_counter < BLOCK_SIZE + 1 then
                 word_counter <= word_counter + 1;
             else
                 word_counter <= 0;
             end if;
         else
             word_counter <= 0;
         end if;
     end if;
 end process;

-- proceso que se encarga de los cambios entre estados
 process(current_state, cpu_enable, cpu_read, hit_detected,
         miss_detected, word_counter)
 begin
     case current_state is
          -- si el estado actual es IDLE, solo pasa a CHECK_HIT si la señal de leer en memoria esta activada y está activada la señal de operaciones en memoria
         when IDLE =>
             if cpu_enable = '1' and cpu_read = '1' then
                 next_state <= CHECK_HIT;
             else
                 next_state <= IDLE;
             end if;
        -- si el estado es CHECK_HIT pasa a READ_MISS si hay un miss  y pasa a IDLE si hay un hit
        -- en cualquier otro caso para a IDLE
         when CHECK_HIT =>
             if hit_detected = '1' then
                 next_state <= IDLE;
             elsif miss_detected = '1' then
                 next_state <= READ_MISS;
             else
                 next_state <= IDLE;
             end if;
        -- si el estado actual es READ_MISS pasa a ALLOCATE si el contador de operaciones de bloque es mayor o igual al tamaño del bloque + 1, y se mantiene en READ_MISS en caso contrario
         when READ_MISS =>
             if word_counter >= BLOCK_SIZE + 1 then
                 next_state <= ALLOCATE;
             else
                 next_state <= READ_MISS;
             end if;
        -- si el estado actual es ALLOCATE pasa a IDLE incondicionalmente
         when ALLOCATE =>
             next_state <= IDLE;
        -- el estado por defecto es IDLE
         when others =>
             next_state <= IDLE;
     end case;
 end process;

-- proceso que se encarga de la logica de cada estado
 process(clk, reset)
     variable temp_block : cache_block;
     variable line : line;
 begin
     if reset = '1' then
         -- Inicializar todos los datos
         for i in 0 to CACHE_SIZE-1 loop
             cache_mem(i).valid <= '0';
             cache_mem(i).tag <= (others => '0');
             for j in 0 to BLOCK_SIZE-1 loop
                 cache_mem(i).data(j) <= (others => '0');
             end loop;
         end loop;
         for j in 0 to BLOCK_SIZE-1 loop
             read_data_buffer(j) <= (others => '0');
         end loop;
         ram_address <= (others => '0');
         ram_read_internal <= '0';
         cpu_instruction <= (others => '0');
     elsif rising_edge(clk) then
         ram_read_internal <= '0';
      
         case current_state is
             -- logica del estado IDLE
             when IDLE =>
                -- no pasa nada
                 ram_address <= (others => '0');
            -- logica del estado CHECK_HIT
             when CHECK_HIT =>
                -- si hay hit y esta activada la bandera de lectura de memoria se devuelve el dato que indique el indice
                 if hit_detected = '1' and cpu_read = '1' then
                     cpu_instruction <= current_block.data(offset_int);
                     -- prints
                     if monitor_enable = '1' then
                         write(line, string'("Estado CHECK_HIT, direccion "));
                         write(line, slv_to_string(cpu_address));
                         write(line, string'(" Instruccion "));
                         write(line, slv_to_string(current_block.data(offset_int)));
                         writeline(output, line);
                     end if;
                 end if;
            -- logica del estado READ_MISS
             when READ_MISS =>
                 if word_counter < BLOCK_SIZE then
                     -- se piden las 8 palabras a la ram
                     ram_address <= std_logic_vector(unsigned(block_initial_addr) + to_unsigned(word_counter, 14));
                     ram_read_internal <= '1';
                    -- prints
                     if monitor_enable = '1' then
                         write(line, string'("Estado READ_MISS, pidiendo palabra "));
                         write(line, word_counter);
                         write(line, string'(" direccion "));
                         write(line, slv_to_string(std_logic_vector(unsigned(block_initial_addr) + to_unsigned(word_counter, 14))));
                         writeline(output, line);
                     end if;
                 end if;
              
                -- traer datos con 2 ciclos de retraso
                -- la ram tarda 2 ciclos en traer los datos, entonces por eso hay un retraso
                 if word_counter >= 2 and word_counter <= BLOCK_SIZE + 1 then
                     read_data_buffer(word_counter - 2) <= ram_data_to_write;
                  
                     if monitor_enable = '1' then
                         write(line, string'("Almacenando indice "));
                         write(line, word_counter - 2);
                         write(line, string'(" instruccion "));
                         write(line, slv_to_string(ram_data_to_write));
                         writeline(output, line);
                     end if;
                 end if;
              
                 if monitor_enable = '1' and word_counter = 0 then
                     write(line, string'("Leyendo bloque "));
                     write(line, index_int);
                     write(line, string'(" Tag "));
                     write(line, slv_to_string(addr_tag));
                     writeline(output, line);
                 end if;
            -- logica del estado ALLOCATE
             when ALLOCATE =>
                -- se carga lo que haya en el buffer en el bloque de la cache correspondiente
                 temp_block := cache_mem(index_int);
                 temp_block.data := read_data_buffer;
                -- se actualizan los valid, dirty y tag bit
                 temp_block.valid := '1';
                 temp_block.tag := addr_tag;
                 cache_mem(index_int) <= temp_block;
              
                 -- retornar la instruccion solicitada
                 cpu_instruction <= read_data_buffer(offset_int);
                 -- prints
                 if monitor_enable = '1' then
                     write(line, string'("Estado ALLOCATE: Bloque "));
                     write(line, index_int);
                     write(line, string'(" Tag "));
                     write(line, slv_to_string(addr_tag));
                     write(line, string'(" Instrucciones "));
                     write(line, BLOCK_SIZE);
                     writeline(output, line);
                 end if;
              
             when others =>
                 null;
         end case;
     end if;
 end process;

end Behavioral;

// VHDL entity address_balancer, as the project stores it:
library IEEE;
use IEEE.STD_LOGIC_1164.ALL;
use IEEE.NUMERIC_STD.ALL;

entity address_balancer is
    Port ( 
        addrC1 : in STD_LOGIC_VECTOR (13 downto 0);
        addrC2 : in STD_LOGIC_VECTOR (13 downto 0);
        finalAddrC1 : out STD_LOGIC_VECTOR (13 downto 0);
        finalAddrC2 : out STD_LOGIC_VECTOR (13 downto 0)
    );
end address_balancer;

architecture Behavioral of address_balancer is
    -- Signals for addrC1 processing
    signal quotient1 : unsigned(10 downto 0);  -- 14-bit / 8 = max 11 bits
    signal quotient1_lsb : std_logic;
    signal addrC1_unsigned : unsigned(13 downto 0);
    signal result1 : unsigned(13 downto 0);
    
    -- Signals for addrC2 processing
    signal quotient2 : unsigned(10 downto 0);  -- 14-bit / 8 = max 11 bits
    signal quotient2_lsb : std_logic;
    signal addrC2_unsigned : unsigned(13 downto 0);
    signal result2 : unsigned(13 downto 0);
begin
    -- Convert inputs to unsigned
    addrC1_unsigned <= unsigned(addrC1);
    addrC2_unsigned <= unsigned(addrC2);
    
    -- Division by 8 for both inputs (right shift by 3)
    quotient1 <= addrC1_unsigned(13 downto 3);
    quotient2 <= addrC2_unsigned(13 downto 3);
    
    -- Check if quotients are odd (LSB = '1')
    quotient1_lsb <= quotient1(0);
    quotient2_lsb <= quotient2(0);
    
    -- Conditional addition process for addrC1 (add 8 if odd quotient)
    process(addrC1_unsigned, quotient1_lsb)
    begin
        if quotient1_lsb = '1' then
            -- Quotient is odd, add 8 to input
            result1 <= addrC1_unsigned + 8;
        else
            -- Quotient is even, output input unchanged
            result1 <= addrC1_unsigned;
        end if;
    end process;
    
    -- Conditional addition process for addrC2 (add 8 if even quotient)
    process(addrC2_unsigned, quotient2_lsb)
    begin
        if quotient2_lsb = '0' then
            -- Quotient is even, add 8 to input
            result2 <= addrC2_unsigned + 8;
        else
            -- Quotient is odd, output input unchanged
            result2 <= addrC2_unsigned;
        end if;
    end process;
    
    -- Convert results back to std_logic_vector
    finalAddrC1 <= std_logic_vector(result1);
    finalAddrC2 <= std_logic_vector(result2);

end Behavioral;
