// Logisim project Circuito.circ as structural Verilog
// clock
module main (
);

  wire and_1_out, and_2_out, and_3_out, and_4_out, branch_taken, can_write_ra, can_write_ra2_q, clock,
       comparator_1_gt, comparator_2_eq, comparator_3_eq, comparator_4_eq, comparator_5_eq, comparator_8_eq,
       comparator_9_eq, decoder_1_out0, decoder_1_out1, decoder_1_out2, decoder_1_out3, decoder_1_out4,
       decoder_1_out5, decoder_1_out6, decoder_1_out7, decoder_1_out8, decoder_1_out9, decoder_1_out10,
       decoder_1_out11, decoder_1_out14, load_enable, multiplexer_2_out, register_2_q, RewritePC,
       store_enable, SystemCall, undriven, Write;
  wire [2:0] InstFetch_q_3;
  wire [4:0] Destino, Destino2_q, Destino3_q, InstFetch_q_2, InstFetch_q_4, InstFetch_q_5, mem_OpCode_q,
       OpCode2_q, OpCode3_q, translator_1_translatedc;
  wire [6:0] InstFetch_q, InstFetch_q_6;
  wire [11:0] jalr_offset_q;
  wire [12:0] branch_offset_q, multiplier_2_out;
  wire [13:0] addr_calculator_1_addr, addr_in, branch_jump_1_next_pc, PC_Actual;
  wire [20:0] jal_offset_q, multiplier_1_out;
  wire [31:0] base_position, Instruction01_q, load_offset, load_result, mem_Resultado_q, ModifiedPC,
       multiplexer_1_out, multiplexer_3_out, multiplexer_4_out, multiplexer_5_out, multiplexer_6_out,
       multiplexer_7_out, multiplexer_8_out, multiplexer_9_out, NewPC, ram_1_dout, register_1_q, Regs_op1,
       Regs_op2, Resultado_q, return_address, return_address2_q, store_offset, store_write_data,
       store_write_in, WriteData;

  Multiplexer #(.width(32)) multiplexer_1 (.in0(NewPC), .in1(ModifiedPC), .out(multiplexer_1_out), .sel(branch_taken));
  Multiplexer multiplexer_2 (.in0(RewritePC), .in1(branch_taken), .out(multiplexer_2_out), .sel(branch_taken));
  Counter #(.max('h3fff), .width(14)) counter_1 (
    .load(multiplexer_2_out), .clk(clock), .D(multiplexer_1_out[13:0]), .Q(PC_Actual));  // open: clr, up, count, carry
  RAM #(.addrWidth(14), .dataWidth(32)) ram_1 (.addr(PC_Actual), .clk(clock), .dout(ram_1_dout));  // open: we, oe, din
  RAM #(.addrWidth(14), .dataWidth(32)) ram_2 (
    .addr(addr_in), .we(store_enable), .oe(load_enable), .clk(clock), .din(store_write_in), .dout(load_result));
  Register #(.width(32)) InstFetch (
    .D(ram_1_dout), .clk(clock),
    .Q({InstFetch_q_6, InstFetch_q_2, InstFetch_q_4, InstFetch_q_3, InstFetch_q_5, InstFetch_q}));  // open: en, clr
  Clock clock_1 (.out(clock));
  Comparator #(.width(5)) comparator_1 (.a(Destino2_q), .b({5{1'b0}}), .gt(comparator_1_gt));  // open: eq, lt
  Comparator #(.width(5)) comparator_2 (.a(InstFetch_q_4), .b(Destino2_q), .eq(comparator_2_eq));  // open: gt, lt
  Comparator #(.width(5)) comparator_3 (.a(InstFetch_q_2), .b(Destino2_q), .eq(comparator_3_eq));  // open: gt, lt
  Translator translator_1 (
    .opCode(InstFetch_q), .funct3(InstFetch_q_3), .funct7(InstFetch_q_6),
    .TranslatedC(translator_1_translatedc));
  Registros Regs (
    .clk(clock), .writeDestiny(Destino), .writeEnable(Write), .nOp1(InstFetch_q_4), .nOp2(InstFetch_q_2),
    .writeData(WriteData), .op2(Regs_op2), .op1(Regs_op1));
  and and_1 (and_1_out, comparator_2_eq, comparator_1_gt);
  and and_2 (and_2_out, comparator_3_eq, comparator_1_gt);
  Multiplier #(.width(21)) multiplier_1 (
    .a({1'b0, InstFetch_q_6[6], InstFetch_q_4, InstFetch_q_3, InstFetch_q_2[0], InstFetch_q_6[5:0], InstFetch_q_2[4:1]}),
    .b(21'h2), .out(multiplier_1_out));  // open: cin, cout
  Multiplier #(.width(13)) multiplier_2 (
    .a({InstFetch_q_6[6], InstFetch_q_5[0], InstFetch_q_6[5:0], InstFetch_q_5[4:1], 1'b0}), .b(13'h2),
    .out(multiplier_2_out));  // open: cin, cout
  Comparator #(.width(5)) comparator_4 (.a(InstFetch_q_4), .b(Destino3_q), .eq(comparator_4_eq));  // open: gt, lt
  Comparator #(.width(5)) comparator_5 (.a(InstFetch_q_2), .b(Destino3_q), .eq(comparator_5_eq));  // open: gt, lt
  and and_3 (and_3_out, comparator_4_eq, comparator_1_gt);
  and and_4 (and_4_out, comparator_5_eq, comparator_1_gt);
  Multiplexer #(.width(32)) multiplexer_3 (.in0(Regs_op1), .in1(NewPC), .out(multiplexer_3_out), .sel(and_1_out));
  Multiplexer #(.width(32)) multiplexer_4 (.in0(Regs_op2), .in1(NewPC), .out(multiplexer_4_out), .sel(and_2_out));
  Multiplexer #(.width(32)) multiplexer_5 (
    .in0(multiplexer_3_out), .in1(Resultado_q), .out(multiplexer_5_out), .sel(and_3_out));
  Multiplexer #(.width(32)) multiplexer_6 (
    .in0(multiplexer_4_out), .in1(Resultado_q), .out(multiplexer_6_out), .sel(and_4_out));
  Register #(.width(12)) jalr_offset (
    .D({InstFetch_q_6, InstFetch_q_2}), .clk(clock), .Q(jalr_offset_q));  // open: en, clr
  Register #(.width(21)) jal_offset (.D(multiplier_1_out), .clk(clock), .Q(jal_offset_q));  // open: en, clr
  Register #(.width(13)) branch_offset (.D(multiplier_2_out), .clk(clock), .Q(branch_offset_q));  // open: en, clr
  Register #(.width(32)) Instruction01 (
    .D({InstFetch_q_6, InstFetch_q_2, InstFetch_q_4, InstFetch_q_3, InstFetch_q_5, InstFetch_q}),
    .clk(clock), .Q(Instruction01_q));  // open: en, clr
  Register #(.width(32)) store_offset_2 (
    .D({{20{1'b0}}, InstFetch_q_6, InstFetch_q_5}), .clk(clock), .Q(store_offset));  // open: en, clr
  Register #(.width(5)) OpCode2 (.D(translator_1_translatedc), .clk(clock), .Q(OpCode2_q));  // open: en, clr
  Register #(.width(5)) Destino2 (.D(InstFetch_q_5), .clk(clock), .Q(Destino2_q));  // open: en, clr
  Register #(.width(32)) Op1 (.D(multiplexer_5_out), .clk(clock), .Q(base_position), .clr(undriven));  // open: en
  Register #(.width(32)) Op2 (.D(multiplexer_6_out), .clk(clock), .Q(store_write_data));  // open: en, clr
  Register #(.width(32)) Imm2 (
    .D({{20{1'b0}}, InstFetch_q_6, InstFetch_q_2}), .clk(clock), .Q(load_offset));  // open: en, clr
  Comparator #(.width(5)) comparator_6 (.a(OpCode2_q), .b(5'b10011), .eq(RewritePC));  // open: gt, lt
  Multiplexer #(.width(32)) multiplexer_7 (
    .in0(base_position), .in1({{18{1'b0}}, PC_Actual}), .out(multiplexer_7_out), .sel(RewritePC));
  branch_jump branch_jump_1 (
    .opcode(OpCode2_q), .op1(base_position), .op2(store_write_data), .branch_offset(branch_offset_q),
    .jump_offset(jal_offset_q), .jalr_rs1(base_position), .jalr_offset(jalr_offset_q),
    .current_pc(PC_Actual), .rd_write_en(can_write_ra), .rd_data(return_address),
    .next_pc(branch_jump_1_next_pc), .branch_taken(branch_taken));
  assign ModifiedPC = {{18{branch_jump_1_next_pc[13]}}, branch_jump_1_next_pc};  // Bit_Extender bit_extender_1
  Comparator #(.width(5)) comparator_7 (.a(OpCode2_q), .b(5'b10100), .eq(SystemCall));  // open: gt, lt
  ALU ALU1 (.opCode(OpCode2_q), .op1(multiplexer_7_out), .op2(store_write_data), .imm(load_offset), .result(NewPC));
  LED led_1 (.in(SystemCall));
  Multiplexer #(.select(5), .width(32)) multiplexer_8 (
    .in0(NewPC), .in1(NewPC), .in2(NewPC), .in3(NewPC), .in4(NewPC), .in5(NewPC), .in6(NewPC), .in7(NewPC),
    .in8(NewPC), .in9(NewPC), .in10(NewPC), .in11(NewPC), .in14(NewPC), .in15(NewPC),
    .out(multiplexer_8_out), .sel(OpCode2_q));  // open: in12, in13, in16, in17, in18, in19, in20, in21, in22, in23, in24, in25, in26, in27, in28, in29, in30, in31
  addr_calculator addr_calculator_1 (
    .store_offset(store_offset), .load_offset(load_offset), .op_code_alu(OpCode2_q), .base(base_position),
    .addr(addr_calculator_1_addr));
  Register #(.width(32)) Instruction02 (.D(Instruction01_q), .clk(clock));  // open: en, Q, clr
  Register #(.width(32)) store_data (.D(store_write_data), .clk(clock), .Q(store_write_in));  // open: en, clr
  Register #(.width(14)) store_addr (.D(addr_calculator_1_addr), .clk(clock), .Q(addr_in));  // open: en, clr
  Register #(.width(5)) OpCode3 (.D(OpCode2_q), .clk(clock), .Q(OpCode3_q));  // open: en, clr
  Register #(.width(5)) Destino3 (.D(Destino2_q), .clk(clock), .Q(Destino3_q));  // open: en, clr
  Register #(.width(32)) Resultado (.D(multiplexer_8_out), .clk(clock), .Q(Resultado_q));  // open: en, clr
  Register #(.width(32)) register_1 (.D(return_address), .clk(clock), .Q(register_1_q));  // open: en, clr
  Register #(.width(1)) register_2 (.D(can_write_ra), .clk(clock), .Q(register_2_q));  // open: en, clr
  Register #(.width(5)) mem_OpCode (.D(OpCode3_q), .clk(clock), .Q(mem_OpCode_q));  // open: en, clr
  Register #(.width(5)) mem_Destino (.D(Destino3_q), .clk(clock), .Q(Destino));  // open: en, clr
  Register #(.width(32)) mem_Resultado (.D(Resultado_q), .clk(clock), .Q(mem_Resultado_q));  // open: en, clr
  Register #(.width(32)) return_address2 (.D(register_1_q), .clk(clock), .Q(return_address2_q));  // open: en, clr
  Register #(.width(1)) can_write_ra2 (.D(register_2_q), .clk(clock), .Q(can_write_ra2_q));  // open: en, clr
  Decoder #(.select(5)) decoder_1 (
    .out0(decoder_1_out0), .out1(decoder_1_out1), .out2(decoder_1_out2), .out3(decoder_1_out3),
    .out4(decoder_1_out4), .out5(decoder_1_out5), .out6(decoder_1_out6), .out7(decoder_1_out7),
    .out8(decoder_1_out8), .out9(decoder_1_out9), .out10(decoder_1_out10), .out11(decoder_1_out11),
    .out12(load_enable), .out13(store_enable), .out14(decoder_1_out14), .sel(OpCode3_q));  // open: out15, out16, out17, out18, out19, out20, out21, out22, out23, out24, out25, out26, out27, out28, out29, out30, out31, en
  Multiplexer #(.width(32)) multiplexer_9 (
    .in0(mem_Resultado_q), .in1(load_result), .out(multiplexer_9_out), .sel(comparator_8_eq));
  Comparator #(.width(5)) comparator_8 (.a(mem_OpCode_q), .b(5'b01100), .eq(comparator_8_eq));  // open: gt, lt
  Comparator #(.mode("unsigned"), .width(5)) comparator_9 (
    .a(mem_OpCode_q), .b(5'b01101), .eq(comparator_9_eq));  // open: gt, lt
  not not_1 (Write, comparator_9_eq);
  Multiplexer #(.width(32)) multiplexer_10 (
    .in0(multiplexer_9_out), .in1(return_address2_q), .out(WriteData), .sel(can_write_ra2_q));
  // OR_Gate or_1 has open pins: in1=decoder_1_out14, in2=load_enable, in3=decoder_1_out11, in4=decoder_1_out10, in5=decoder_1_out9, in6=decoder_1_out8, in7=decoder_1_out7, in8=decoder_1_out6, in9=decoder_1_out5, in10=decoder_1_out4, in11=decoder_1_out3, in12=decoder_1_out2, in13=decoder_1_out1, in14=decoder_1_out0, out=open

  // Notes on the sheet:
  //   Esto se va a convertir en cache, es temporal
  //   Esto se va a convertir en cache, es temporal
  //   Dependiendo de la instruccion, algo diferente tiene que salir
  //   Registro al que se escribira
  //   Datos a escribir en registro
  //   Este decoder nos dice si una instruccion escribe en registro
  //   Decide si debe escribirse algo en registro
  //   Puede que haya leido mal, entonces dejo el decoder aqui
  //   Viendo las instrucciones, parece que solo el SW (13 / 0d) no escribe en un registro
endmodule

module Registros (
  input  [4:0] nOp1,
  input  [4:0] nOp2,
  input  [31:0] writeData,
  input  [4:0] writeDestiny,
  input  writeEnable,
  input  clk,
  output [31:0] op1,
  output [31:0] op2
);

  wire decoder_1_out1, decoder_1_out2, decoder_1_out3, decoder_1_out4, decoder_1_out5, decoder_1_out6,
       decoder_1_out7, decoder_1_out8, decoder_1_out9, decoder_1_out10, decoder_1_out11, decoder_1_out12,
       decoder_1_out13, decoder_1_out14, decoder_1_out15, decoder_1_out16, decoder_1_out17, decoder_1_out18,
       decoder_1_out19, decoder_1_out20, decoder_1_out21, decoder_1_out22, decoder_1_out24, decoder_1_out25,
       decoder_1_out26, decoder_1_out27, decoder_1_out28, decoder_1_out29, decoder_1_out30, decoder_1_out31,
       not_1_out;
  wire [4:0] multiplexer_1_out;
  wire [31:0] x0_q, x1_q, x2_q, x3_q, x4_q, x5_q, x6_q, x7_q, x8_q, x9_q, x10_q, x11_q, x12_q, x13_q, x14_q,
       x15_q, x16_q, x17_q, x18_q, x19_q, x20_q, x21_q, x22_q, x23_q, x24_q, x25_q, x26_q, x27_q, x28_q,
       x29_q, x30_q, x31_q;

  not not_1 (not_1_out, writeEnable);
  Decoder #(.select(5)) decoder_1 (
    .out1(decoder_1_out1), .out2(decoder_1_out2), .out3(decoder_1_out3), .out4(decoder_1_out4),
    .out5(decoder_1_out5), .out6(decoder_1_out6), .out7(decoder_1_out7), .out8(decoder_1_out8),
    .out9(decoder_1_out9), .out10(decoder_1_out10), .out11(decoder_1_out11), .out12(decoder_1_out12),
    .out13(decoder_1_out13), .out14(decoder_1_out14), .out15(decoder_1_out15), .out16(decoder_1_out16),
    .out17(decoder_1_out17), .out18(decoder_1_out18), .out19(decoder_1_out19), .out20(decoder_1_out20),
    .out21(decoder_1_out21), .out22(decoder_1_out22), .out23(decoder_1_out7), .out24(decoder_1_out24),
    .out25(decoder_1_out25), .out26(decoder_1_out26), .out27(decoder_1_out27), .out28(decoder_1_out28),
    .out29(decoder_1_out29), .out30(decoder_1_out30), .out31(decoder_1_out31), .sel(multiplexer_1_out));  // open: out0, en
  Multiplexer #(.width(5)) multiplexer_1 (
    .in0(writeDestiny), .in1({5{1'b0}}), .out(multiplexer_1_out), .sel(not_1_out));
  Register #(.width(32)) x0 (.D(writeData), .Q(x0_q));  // open: en, clk, clr
  Register #(.width(32)) x1 (.D(writeData), .en(decoder_1_out1), .clk(clk), .Q(x1_q));  // open: clr
  Register #(.width(32)) x2 (.D(writeData), .en(decoder_1_out2), .clk(clk), .Q(x2_q));  // open: clr
  Register #(.width(32)) x3 (.D(writeData), .en(decoder_1_out3), .clk(clk), .Q(x3_q));  // open: clr
  Register #(.width(32)) x4 (.D(writeData), .en(decoder_1_out4), .clk(clk), .Q(x4_q));  // open: clr
  Register #(.width(32)) x5 (.D(writeData), .en(decoder_1_out5), .clk(clk), .Q(x5_q));  // open: clr
  Register #(.width(32)) x6 (.D(writeData), .en(decoder_1_out6), .clk(clk), .Q(x6_q));  // open: clr
  Register #(.width(32)) x7 (.D(writeData), .en(decoder_1_out7), .clk(clk), .Q(x7_q));  // open: clr
  Register #(.width(32)) x8 (.D(writeData), .en(decoder_1_out8), .clk(clk), .Q(x8_q));  // open: clr
  Register #(.width(32)) x9 (.D(writeData), .en(decoder_1_out9), .clk(clk), .Q(x9_q));  // open: clr
  Register #(.width(32)) x10 (.D(writeData), .en(decoder_1_out10), .clk(clk), .Q(x10_q));  // open: clr
  Register #(.width(32)) x11 (.D(writeData), .en(decoder_1_out11), .clk(clk), .Q(x11_q));  // open: clr
  Register #(.width(32)) x12 (.D(writeData), .en(decoder_1_out12), .clk(clk), .Q(x12_q));  // open: clr
  Register #(.width(32)) x13 (.D(writeData), .en(decoder_1_out13), .clk(clk), .Q(x13_q));  // open: clr
  Register #(.width(32)) x14 (.D(writeData), .en(decoder_1_out14), .clk(clk), .Q(x14_q));  // open: clr
  Register #(.width(32)) x15 (.D(writeData), .en(decoder_1_out15), .clk(clk), .Q(x15_q));  // open: clr
  Multiplexer #(.select(5), .width(32)) multiplexer_2 (
    .in0(x0_q), .in1(x1_q), .in2(x2_q), .in3(x3_q), .in4(x4_q), .in5(x5_q), .in6(x6_q), .in7(x7_q),
    .in8(x8_q), .in9(x9_q), .in10(x10_q), .in11(x11_q), .in12(x12_q), .in13(x13_q), .in14(x14_q),
    .in15(x15_q), .in16(x16_q), .in17(x17_q), .in18(x18_q), .in19(x19_q), .in20(x20_q), .in21(x21_q),
    .in22(x22_q), .in23(x23_q), .in24(x24_q), .in25(x25_q), .in26(x26_q), .in27(x27_q), .in28(x28_q),
    .in29(x29_q), .in30(x30_q), .in31(x31_q), .out(op1), .sel(nOp1));
  Multiplexer #(.select(5), .width(32)) multiplexer_3 (
    .in0(x0_q), .in1(x1_q), .in2(x2_q), .in3(x3_q), .in4(x4_q), .in5(x5_q), .in6(x6_q), .in7(x7_q),
    .in8(x8_q), .in9(x9_q), .in10(x10_q), .in11(x11_q), .in12(x12_q), .in13(x13_q), .in14(x14_q),
    .in15(x15_q), .in16(x16_q), .in17(x17_q), .in18(x18_q), .in19(x19_q), .in20(x20_q), .in21(x21_q),
    .in22(x22_q), .in23(x23_q), .in24(x24_q), .in25(x25_q), .in26(x26_q), .in27(x27_q), .in28(x28_q),
    .in29(x29_q), .in30(x30_q), .in31(x31_q), .out(op2), .sel(nOp2));
  Register #(.width(32)) x16 (.D(writeData), .en(decoder_1_out16), .clk(clk), .Q(x16_q));  // open: clr
  Register #(.width(32)) x17 (.D(writeData), .en(decoder_1_out17), .clk(clk), .Q(x17_q));  // open: clr
  Register #(.width(32)) x18 (.D(writeData), .en(decoder_1_out18), .clk(clk), .Q(x18_q));  // open: clr
  Register #(.width(32)) x19 (.D(writeData), .en(decoder_1_out19), .clk(clk), .Q(x19_q));  // open: clr
  Register #(.width(32)) x20 (.D(writeData), .en(decoder_1_out20), .clk(clk), .Q(x20_q));  // open: clr
  Register #(.width(32)) x21 (.D(writeData), .en(decoder_1_out21), .clk(clk), .Q(x21_q));  // open: clr
  Register #(.width(32)) x22 (.D(writeData), .en(decoder_1_out22), .clk(clk), .Q(x22_q));  // open: clr
  Register #(.width(32)) x23 (.D(writeData), .en(decoder_1_out7), .clk(clk), .Q(x23_q));  // open: clr
  Register #(.width(32)) x24 (.D(writeData), .en(decoder_1_out24), .clk(clk), .Q(x24_q));  // open: clr
  Register #(.width(32)) x25 (.D(writeData), .en(decoder_1_out25), .clk(clk), .Q(x25_q));  // open: clr
  Register #(.width(32)) x26 (.D(writeData), .en(decoder_1_out26), .clk(clk), .Q(x26_q));  // open: clr
  Register #(.width(32)) x27 (.D(writeData), .en(decoder_1_out27), .clk(clk), .Q(x27_q));  // open: clr
  Register #(.width(32)) x28 (.D(writeData), .en(decoder_1_out28), .clk(clk), .Q(x28_q));  // open: clr
  Register #(.width(32)) x29 (.D(writeData), .en(decoder_1_out29), .clk(clk), .Q(x29_q));  // open: clr
  Register #(.width(32)) x30 (.D(writeData), .en(decoder_1_out30), .clk(clk), .Q(x30_q));  // open: clr
  Register #(.width(32)) x31 (.D(writeData), .en(decoder_1_out31), .clk(clk), .Q(x31_q));  // open: clr
endmodule

module addr_calculator (
  input  [31:0] store_offset,
  input  [31:0] load_offset,
  input  [4:0] op_code_alu,
  input  [31:0] base,
  output [13:0] addr
);

  wire comparator_1_eq;
  wire [31:0] multiplexer_1_out;
  wire [31:14] adder_1_out;

  Comparator #(.width(5)) comparator_1 (.a(op_code_alu), .b(5'b01100), .eq(comparator_1_eq));  // open: gt, lt
  Multiplexer #(.width(32)) multiplexer_1 (
    .in0(store_offset), .in1(load_offset), .out(multiplexer_1_out), .sel(comparator_1_eq));
  Adder #(.width(32)) adder_1 (.a(multiplexer_1_out), .b(base), .out({adder_1_out, addr}));  // open: cin, cout
endmodule

// VHDL entity not_gate, as the project stores it:
library IEEE;
use IEEE.STD_LOGIC_1164.ALL;

entity not_gate is
    Port ( 
        input  : in  STD_LOGIC;
        output : out STD_LOGIC
    );
end not_gate;

architecture behavioral of not_gate is
begin
    output <= not input;
end behavioral;

// VHDL entity ALU, as the project stores it:
LIBRARY ieee;
USE ieee.std_logic_1164.all;
USE ieee.numeric_std.all;

ENTITY ALU IS
  PORT (
    	opCode	: IN std_logic_vector(4 DOWNTO 0); -- codigo de operacion (5 bits)
	op1		: IN std_logic_vector(31 DOWNTO 0); -- operando 1 (32 bits)
	op2		: IN std_logic_vector(31 DOWNTO 0); -- operando 2 (32 bits)
    	imm		: IN std_logic_vector(31 DOWNTO 0); -- immediato (32 bits)
    	result   	: OUT std_logic_vector(31 DOWNTO 0)  -- resultado de la operacion (32 bits)
  );
END ALU;

--------------------------------------------------------------------------------
-- ALU Architecture Implementation
--------------------------------------------------------------------------------

ARCHITECTURE TypeArchitecture OF ALU IS
BEGIN
    PROCESS(opCode, op1, op2)
    BEGIN
        CASE opCode IS
            WHEN "00000" => -- ADD
                result <= std_logic_vector(signed(op1) + signed(op2));
            
            WHEN "00001" => -- SUB
                result <= std_logic_vector(signed(op1) - signed(op2));
            
            WHEN "00010" => -- ADDI
                result <= std_logic_vector(signed(op1) + signed(imm));
            
            WHEN "00011" => -- AND
                result <= op1 AND op2;
            
            WHEN "00100" => -- OR
                result <= op1 OR op2;
            
            WHEN "00101" => -- XOR
                result <= op1 XOR op2;
            
            WHEN "00110" => -- ANDI
                result <= op1 AND imm;
            
            WHEN "00111" => -- ORI
                result <= op1 OR imm;

            WHEN "01000" => -- XORI
                result <= op1 XOR imm;
            WHEN "01001" => -- SLL (Shift Left Logical)
	        	 result <= std_logic_vector(shift_left(unsigned(op1), to_integer(unsigned(op2(4 DOWNTO 0)))));
	
	       WHEN "01010" => -- SRL (Shift Right Logical)
	        	 result <= std_logic_vector(shift_right(unsigned(op1), to_integer(unsigned(op2(4 DOWNTO 0)))));
	
	       WHEN "01011" => -- SRA (Shift Right Arithmetic)
	        	 result <= std_logic_vector(shift_right(signed(op1), to_integer(unsigned(op2(4 DOWNTO 0)))));
	        
	       WHEN "10010" => -- LUI
	        	result <= std_logic_vector(shift_left(unsigned(imm(11 downto 0)), 12));
	
	       WHEN "10011" => -- AUIPC
	        result <= std_logic_vector(
				        unsigned(op1) + unsigned("000000000000000000" & imm(11 downto 0) & "00")
				    );
            WHEN OTHERS =>
                result <= (OTHERS => '0');
        END CASE;
    END PROCESS;

END TypeArchitecture;

// VHDL entity Translator, as the project stores it:
LIBRARY ieee;
USE ieee.std_logic_1164.all;

ENTITY Translator IS
  PORT (
  ------------------------------------------------------------------------------
  --Insert input ports below
    opCode    	: IN  std_logic_vector(6 DOWNTO 0); -- Op Code que describe el tipo de instruccion
    funct3     	: IN  std_logic_vector(2 DOWNTO 0); -- funct3 que describe la instruccion especifica
    funct7     	: IN  std_logic_vector(6 DOWNTO 0); -- funct7 que describe la instruccion especifica (solo en R-Type)
  ------------------------------------------------------------------------------
  --Insert output ports below
    TranslatedC	: OUT std_logic_vector(4 DOWNTO 0)  -- Codigo traducido
    );
END Translator;

--------------------------------------------------------------------------------
--Complete your VHDL description below
--------------------------------------------------------------------------------

ARCHITECTURE TypeArchitecture OF Translator IS

BEGIN
    PROCESS(opCode, funct3, funct7)
    BEGIN
        CASE opCode IS
            WHEN "0110011" => -- R-Type
                IF funct3 = "000" and funct7 = "0000000" THEN
                	TranslatedC <= "00000"; 
                END IF;
                -- 	SLL
                IF funct3 = "001" and funct7 = "0000000" THEN
                	TranslatedC <= "01001"; 
                END IF;
                --	SRL
                IF funct3 = "101" and funct7 = "0000000" THEN
                	TranslatedC <= "01010"; 
                END IF;
                --	SRA
                IF funct3 = "101" and funct7 = "0100000" THEN
                	TranslatedC <= "01011"; 
                END IF;

		  WHEN "1100011" => -- B-Type
		  	 -- BEQ
                IF funct3 = "000" and funct7 = "0000000" THEN
                	TranslatedC <= "01110"; 
                END IF;
                -- BNE
                IF funct3 = "001" and funct7 = "0000000" THEN
                	TranslatedC <= "01111"; 
                END IF;
                
            WHEN "1101111" => -- jal
                IF funct3 = "000" and funct7 = "0000001" THEN
                	TranslatedC <= "10000"; 
                END IF;
            WHEN "1100111" => -- jalr
                IF funct3 = "000" and funct7 = "0000000" THEN
                	TranslatedC <= "10001"; 
                END IF;
                
            WHEN "0110111" => -- U-Type
                -- 	LUI
                IF funct3 = "101" and funct7 = "0001001" THEN
                	TranslatedC <= "10010"; 
                END IF;

            WHEN "0010111" => -- U-Type 2
                -- 	AUIPC
                IF funct3 = "000" and funct7 = "0001000" THEN
                	TranslatedC <= "10011"; 
                END IF;
 
            WHEN "1110011" => -- I-Type 2
                -- 	ECALL
                IF funct3 = "000" and funct7 = "0000000" THEN
                	TranslatedC <= "10100"; 
                END IF;
            WHEN "0000011" => -- Load
            IF funct3 = "010"  THEN -- sw
                	TranslatedC <= "01100"; 
                END IF;
            WHEN "0100011" => -- S-Type
            	IF funct3 = "010"  THEN -- sw
                	TranslatedC <= "01101"; 
                END IF;
            WHEN OTHERS =>
            	TranslatedC <= "11111";
        END CASE;
    END PROCESS;

END TypeArchitecture;

// VHDL entity branch_jump, as the project stores it:
library IEEE;
use IEEE.STD_LOGIC_1164.ALL;
use IEEE.NUMERIC_STD.ALL;

entity branch_jump is
    port (
        opcode        : in  std_logic_vector(4 downto 0);   -- Opcode (14=beq, 15=bne, 16=jal, 17=jalr)
        op1           : in  std_logic_vector(31 downto 0);  -- Data from rs1 (used by beq/bne)
        op2           : in  std_logic_vector(31 downto 0);  -- Data from rs2 (used by beq/bne)
        branch_offset : in  std_logic_vector(12 downto 0);  -- Offset for branches (signed, 13-bit)
        jump_offset   : in  std_logic_vector(20 downto 0);  -- Offset for jumps (signed, 21-bit)
        jalr_rs1      : in  std_logic_vector(31 downto 0);  -- Base register for JALR
        jalr_offset   : in  std_logic_vector(11 downto 0);  -- Offset for JALR (signed, 12-bit)
        current_pc    : in  std_logic_vector(13 downto 0);  -- Current PC (14-bit)
        rd_write_en   : out std_logic;                      -- Enable write to rd
        rd_data       : out std_logic_vector(31 downto 0);  -- Data to write to rd
        next_pc       : out std_logic_vector(13 downto 0);  -- Next PC value
        branch_taken  : out std_logic                       -- Indicates if branch/jump taken
    );
end branch_jump;

architecture Behavioral of branch_jump is
    -- Opcode constants
    constant OP_BEQ  : std_logic_vector(4 downto 0) := "01110"; -- 14
    constant OP_BNE  : std_logic_vector(4 downto 0) := "01111"; -- 15
    constant OP_JAL  : std_logic_vector(4 downto 0) := "10000"; -- 16
    constant OP_JALR : std_logic_vector(4 downto 0) := "10001"; -- 17

    -- Internal signals
    signal is_beq, is_bne, is_jal, is_jalr : std_logic;
    signal branch_eq, take_branch          : std_logic;
    signal branch_off_ext : std_logic_vector(13 downto 0); -- Extended 13-bit branch offset
    signal jump_off_ext   : std_logic_vector(13 downto 0); -- Truncated extended 21-bit jump offset
    signal jalr_off_ext   : std_logic_vector(13 downto 0); -- Extended 12-bit JALR offset
    signal pc_plus_one    : std_logic_vector(13 downto 0);
begin

    -- Opcode decoding
    is_beq  <= '1' when opcode = OP_BEQ  else '0';
    is_bne  <= '1' when opcode = OP_BNE  else '0';
    is_jal  <= '1' when opcode = OP_JAL  else '0';
    is_jalr <= '1' when opcode = OP_JALR else '0';

    -- Branch condition
    branch_eq <= '1' when op1 = op2 else '0';
    take_branch <= (is_beq and branch_eq) or (is_bne and (not branch_eq));

    -- Sign-extend offsets
    branch_off_ext <= std_logic_vector(resize(signed(branch_offset), 14));
    jump_off_ext   <= std_logic_vector(resize(signed(jump_offset), 14));
    jalr_off_ext   <= std_logic_vector(resize(signed(jalr_offset), 14));

    -- PC + 1
    pc_plus_one <= std_logic_vector(unsigned(current_pc) + 1);

    -- Main logic
    process(opcode, op1, op2, branch_off_ext, jump_off_ext, jalr_off_ext,
            current_pc, take_branch, is_jal, is_jalr, pc_plus_one, jalr_rs1)
        variable jalr_target : unsigned(31 downto 0); -- para jalr
    begin
        -- Default values
        rd_write_en <= '0';
        rd_data <= (others => '0');
        next_pc <= pc_plus_one;
        branch_taken <= '0';

        if take_branch = '1' then
            -- Branch taken (BEQ or BNE)
            next_pc <= std_logic_vector(unsigned(current_pc) + unsigned(branch_off_ext));
            branch_taken <= '1';

        elsif is_jal = '1' then
            -- Jump and link
            rd_write_en <= '1';
            rd_data <= std_logic_vector(resize(unsigned(pc_plus_one), 32));
            next_pc <= std_logic_vector(unsigned(current_pc) + unsigned(jump_off_ext));
            branch_taken <= '1';

        elsif is_jalr = '1' then
            -- Jump and link register
            rd_write_en <= '1';
            rd_data <= std_logic_vector(resize(unsigned(pc_plus_one), 32));
            jalr_target := unsigned(jalr_rs1) + unsigned(jalr_off_ext);
            next_pc <= std_logic_vector(jalr_target(13 downto 0)); -- truncamos a 14 bits
            branch_taken <= '1';
        end if;
    end process;

end Behavioral;
